// Logisim project Guia9.circ as structural Verilog: 2 circuits, main circuit main
module main (
  input  in_1,
  input  [2:0] in_2,
  input  in_3,
  input  [1:0] in_4,
  input  in_5,
  input  [31:0] in_6,
  input  in_7,
  input  [1:0] in_8,
  input  in_9,
  output [4:0] out_10,
  output out_11,
  output out_12,
  output [22:0] out_13,
  output out_14,
  output [7:0] out_15,
  output out_16,
  output out_17,
  output [6:0] out_18
);

  wire not_1_out;

  Subcircuito subcircuito_1 (.in_1(in_1), .in_2(in_3), .out_3(out_11), .out_4(out_12));
  not not_1 (not_1_out, in_8[0]);
  or or_1 (out_18[1], in_8[1], in_8[0]);
  and and_1 (out_18[4], in_8[1], not_1_out);
  _7_Segment_Display u_7_segment_display_1 (
    .g(in_8[1]), .f(in_9), .a(in_8[1]), .b(out_18[1]), .e(out_18[4]), .d(in_8[1]), .c(in_8[0]));  // open: dp

  assign out_10 = {in_4, in_2};
  assign out_13 = in_6[22:0];
  assign out_14 = in_7;
  assign out_15 = in_6[30:23];
  assign out_16 = in_7;
  assign out_17 = in_6[31];
  assign {out_18[6:5], out_18[3:2], out_18[0]} = {in_8[1], in_9, in_8, in_8[1]};

  // Other names for the same wires on the sheet: signal = in_7
endmodule

module Subcircuito (
  input  in_1,
  input  in_2,
  output out_3,
  output out_4
);

  wire clock_1_out;

  Clock clock_1 (.out(clock_1_out));
  D_Flip_Flop d_ff_1 (.clk(clock_1_out), .D(in_1), .Q(out_3));  // open: Qn, preset, en, reset
  D_Flip_Flop d_ff_2 (.clk(clock_1_out), .D(in_2), .Q(out_4));  // open: Qn, preset, en, reset
endmodule
