// Logisim project Guia10GerardoJoseVilledaErazo.circ as structural Verilog: 1 circuit, main circuit main
module main (
  input  [7:0] Datos_de_entrada__0x25_en_binario,
  input  Control_de_entrada,
  input  [15:0] Bus_de_direcciones_C120_en_binario,
  input  Reinicia_todos_los_valores_almacenados,
  input  Control_de_entrada_salida,
  input  \Selección_de_memoria ,
  input  in_7,
  output [7:0] Salida_de_datos
);

  wire \Botón_out , Reloj_2_out, Reloj_out;
  wire [2:0] Counter_q;
  wire [7:0] ram_2_data, Registro_2_q, Registro_3_q, Registro_q;

  Clock Reloj (.out(Reloj_out));
  Counter #(.width(3), .max('h7)) Counter (
    .Q(Counter_q), .clk(Reloj_out), .clr(\Botón_out ));  // open: load, D, count, carry
  Button \Botón  (.out(\Botón_out ));
  Register Registro (.D(Registro_2_q), .en(in_7), .Q(Registro_q));  // open: clk, clr
  Clock Reloj_2 (.out(Reloj_2_out));
  DotMatrix #(.matrixcols(4), .matrixrows(8)) dotmatrix_1 (
    .col0(Registro_q), .col1(Registro_2_q), .col2(Registro_3_q), .col3(ram_2_data));
  Register Registro_2 (.D(Registro_3_q), .en(in_7), .Q(Registro_2_q), .clk(Reloj_out));  // open: clr
  RAM #(.addrWidth(16)) ram_1 (
    .addr(Bus_de_direcciones_C120_en_binario), .data(Salida_de_datos), .sel(\Selección_de_memoria ),
    .clk(Reloj_2_out), .ld(Control_de_entrada_salida), .clr(Reinicia_todos_los_valores_almacenados));
  Register Registro_3 (.D(ram_2_data), .en(in_7), .Q(Registro_3_q), .clk(Reloj_out));  // open: clr
  assign Salida_de_datos = Control_de_entrada ? Datos_de_entrada__0x25_en_binario : 8'bz;  // Controlled_Buffer controlled_buffer_1
  RAM #(.addrWidth(3)) ram_2 (.addr(Counter_q), .data(ram_2_data), .clk(Reloj_out));  // open: sel, ld, clr
endmodule
