// Logisim project guia11.circ as structural Verilog: 5 circuits, main circuit 8-bit ALU
module _8_bit_ALU (
  input  [7:0] A,
  input  [7:0] B,
  input  [1:0] Operacion,
  output [7:0] Resultado
);

  wire [7:0] multiplexer_1_out, n8_bit_and_1_resultado, n8_bit_or_1_resultado, n8_bit_suma_reta_1_resultado;

  _8_bit_AND u_8_bit_and_1 (.A(A), .B(B), .Resultado(n8_bit_and_1_resultado));
  _8_bit_OR u_8_bit_or_1 (.A(A), .B(B), .Resultado(n8_bit_or_1_resultado));
  _8_bit_Suma_Reta u_8_bit_suma_reta_1 (
    .A(A), .B(B), .Add_Sub_Control(Operacion[1]), .Resultado(n8_bit_suma_reta_1_resultado));
  Multiplexer #(.width(8), .enable("false")) multiplexer_1 (
    .in0(n8_bit_and_1_resultado), .in1(n8_bit_or_1_resultado), .out(multiplexer_1_out), .sel(Operacion[1]));
  Multiplexer #(.width(8), .enable("false")) multiplexer_2 (
    .in0(multiplexer_1_out), .in1(n8_bit_suma_reta_1_resultado), .out(Resultado), .sel(Operacion[0]));
endmodule

// AND
module _8_bit_AND (
  input  [7:0] A,
  input  [7:0] B,
  output [7:0] Resultado
);

  and AND (Resultado[0], A[0], B[0]);
  and AND_2 (Resultado[1], A[1], B[1]);
  and AND_3 (Resultado[2], A[2], B[2]);
  and AND_4 (Resultado[3], A[3], B[3]);
  and AND_5 (Resultado[4], A[4], B[4]);
  and AND_6 (Resultado[5], A[5], B[5]);
  and AND_7 (Resultado[6], A[6], B[6]);
  and AND_8 (Resultado[7], A[7], B[7]);
endmodule

// OR
module _8_bit_OR (
  input  [7:0] A,
  input  [7:0] B,
  output [7:0] Resultado
);

  or OR (Resultado[0], A[0], B[0]);
  or OR_2 (Resultado[1], A[1], B[1]);
  or OR_3 (Resultado[2], A[2], B[2]);
  or OR_4 (Resultado[3], A[3], B[3]);
  or OR_5 (Resultado[4], A[4], B[4]);
  or OR_6 (Resultado[5], A[5], B[5]);
  or OR_7 (Resultado[6], A[6], B[6]);
  or OR_8 (Resultado[7], A[7], B[7]);
endmodule

// +
module _1_bit_adicion (
  input  Carril_de_entrada,
  input  A,
  input  B,
  output Resultado,
  output Carril_de_salida
);

  wire AND_2_out, AND_out, xor_1_out;

  and AND (AND_out, A, B);
  xor xor_1 (xor_1_out, A, B);
  or OR (Carril_de_salida, AND_out, AND_2_out);
  and AND_2 (AND_2_out, Carril_de_entrada, xor_1_out);
  xor xor_2 (Resultado, Carril_de_entrada, xor_1_out);
endmodule

// +/-
module _8_bit_Suma_Reta (
  input  Add_Sub_Control,
  input  [7:0] A,
  input  [7:0] B,
  output [7:0] Resultado
);

  wire n1_bit_adicion_1_carril_de_salida, n1_bit_adicion_2_carril_de_salida,
       n1_bit_adicion_3_carril_de_salida, n1_bit_adicion_4_carril_de_salida,
       n1_bit_adicion_5_carril_de_salida, n1_bit_adicion_6_carril_de_salida,
       n1_bit_adicion_7_carril_de_salida, xor_1_out, xor_2_out, xor_3_out, xor_4_out, xor_5_out, xor_6_out,
       xor_7_out, xor_8_out;

  xor xor_1 (xor_1_out, Add_Sub_Control, B[0]);
  xor xor_2 (xor_2_out, Add_Sub_Control, B[1]);
  xor xor_3 (xor_3_out, Add_Sub_Control, B[2]);
  xor xor_4 (xor_4_out, Add_Sub_Control, B[3]);
  xor xor_5 (xor_5_out, Add_Sub_Control, B[4]);
  xor xor_6 (xor_6_out, Add_Sub_Control, B[5]);
  xor xor_7 (xor_7_out, Add_Sub_Control, B[6]);
  xor xor_8 (xor_8_out, Add_Sub_Control, B[7]);
  _1_bit_adicion u_1_bit_adicion_1 (
    .A(A[0]), .B(xor_1_out), .Carril_de_entrada(Add_Sub_Control),
    .Carril_de_salida(n1_bit_adicion_1_carril_de_salida), .Resultado(Resultado[0]));
  _1_bit_adicion u_1_bit_adicion_2 (
    .A(A[1]), .B(xor_2_out), .Carril_de_entrada(n1_bit_adicion_1_carril_de_salida),
    .Carril_de_salida(n1_bit_adicion_2_carril_de_salida), .Resultado(Resultado[1]));
  _1_bit_adicion u_1_bit_adicion_3 (
    .A(A[2]), .B(xor_3_out), .Carril_de_entrada(n1_bit_adicion_2_carril_de_salida),
    .Carril_de_salida(n1_bit_adicion_3_carril_de_salida), .Resultado(Resultado[2]));
  _1_bit_adicion u_1_bit_adicion_4 (
    .A(A[3]), .B(xor_4_out), .Carril_de_entrada(n1_bit_adicion_3_carril_de_salida),
    .Carril_de_salida(n1_bit_adicion_4_carril_de_salida), .Resultado(Resultado[3]));
  _1_bit_adicion u_1_bit_adicion_5 (
    .A(A[4]), .B(xor_5_out), .Carril_de_entrada(n1_bit_adicion_4_carril_de_salida),
    .Carril_de_salida(n1_bit_adicion_5_carril_de_salida), .Resultado(Resultado[4]));
  _1_bit_adicion u_1_bit_adicion_6 (
    .A(A[5]), .B(xor_6_out), .Carril_de_entrada(n1_bit_adicion_5_carril_de_salida),
    .Carril_de_salida(n1_bit_adicion_6_carril_de_salida), .Resultado(Resultado[5]));
  _1_bit_adicion u_1_bit_adicion_7 (
    .A(A[6]), .B(xor_7_out), .Carril_de_entrada(n1_bit_adicion_6_carril_de_salida),
    .Carril_de_salida(n1_bit_adicion_7_carril_de_salida), .Resultado(Resultado[6]));
  _1_bit_adicion u_1_bit_adicion_8 (
    .A(A[7]), .B(xor_8_out), .Carril_de_entrada(n1_bit_adicion_7_carril_de_salida), .Resultado(Resultado[7]));  // open: Carril_de_salida
endmodule
