// Logisim project ejemplo.circ as structural Verilog: 1 circuit, main circuit COMPUERTA NOR
module COMPUERTA_NOR (
  input  in_1,
  input  in_2,
  input  in_3,
  input  in_4,
  input  in_5,
  input  in_6,
  input  in_7,
  input  in_8,
  input  in_9,
  input  in_10,
  input  in_11,
  input  in_12,
  input  in_13,
  input  in_14,
  input  in_15,
  input  in_16,
  input  in_17,
  input  in_18,
  input  in_19,
  input  in_20,
  input  in_21,
  input  in_22,
  input  in_23,
  input  in_24,
  input  in_25,
  input  in_26,
  input  in_27,
  input  in_28,
  input  in_29,
  input  in_30,
  input  in_31,
  input  in_32,
  input  in_33,
  input  in_34,
  input  in_35,
  input  in_36,
  input  in_37,
  input  in_38,
  input  in_39,
  input  in_40,
  input  in_41,
  input  in_42,
  input  in_43,
  input  in_44,
  input  in_45,
  input  in_46,
  input  in_47,
  input  in_48,
  input  in_49,
  input  in_50,
  output out_51,
  output out_52,
  output out_53,
  output out_54,
  output out_55,
  output out_56,
  output out_57,
  output out_58,
  output out_59,
  output out_60,
  output out_61,
  output out_62,
  output out_63,
  output out_64,
  output out_65,
  output out_66,
  output out_67,
  output out_68,
  output out_69,
  output out_70,
  output out_71,
  output out_72,
  output out_73,
  output out_74,
  output out_75,
  output out_76
);

  and and_1 (out_51, in_1, in_3);
  and and_2 (out_53, in_5, in_7);
  or or_1 (out_55, in_9, in_11);
  or or_2 (out_57, in_13, in_15);
  not not_1 (out_59, in_17);
  not not_2 (out_60, in_18);
  xor xor_1 (out_61, in_19, in_21);
  xor xor_2 (out_63, in_23, in_25);
  nand nand_1 (out_66, in_28, in_30);
  nand nand_2 (out_67, in_31, in_33);
  nor nor_1 (out_70, in_36, in_38);
  nor nor_2 (out_71, in_39, in_41);
  xnor xnor_1 (out_73, in_43, in_45);
  xnor xnor_2 (out_75, in_47, in_49);
  and and_3 (out_52, in_2, in_4);
  and and_4 (out_54, in_6, in_8);
  or or_3 (out_56, in_10, in_12);
  or or_4 (out_58, in_14, in_16);
  xor xor_3 (out_62, in_20, in_22);
  xor xor_4 (out_64, in_24, in_26);
  nand nand_3 (out_65, in_27, in_29);
  nand nand_4 (out_68, in_32, in_34);
  nor nor_3 (out_69, in_35, in_37);
  nor nor_4 (out_72, in_40, in_42);
  xnor xnor_3 (out_74, in_44, in_46);
  xnor xnor_4 (out_76, in_48, in_50);

  // Notes on the sheet:
  //   COMPUERTA AND
  //   COMPUERTA OR
  //   COMPUERTA XOR
  //   COMPUERTA NAND
  //   COMPUERTA NOT
  //   COMPUERTA NOR
  //   COMPUERTA XNOR
endmodule
