// Logisim project ejercicio.circ as structural Verilog: 1 circuit, main circuit main
module main (
  output [7:0] x_1,
  output [7:0] x
);

  wire clock_1_out;

  Adder adder_1 (.a(8'h1), .b(x), .out(x_1));  // open: cin, cout
  Clock clock_1 (.out(clock_1_out));
  Register register_1 (.D(x_1), .Q(x), .clk(clock_1_out));  // open: en, clr
endmodule
