// Logisim project practica.circ as structural Verilog: 1 circuit, main circuit main
module main (
  input  in_1,
  input  in_2,
  input  in_3,
  input  in_4,
  input  in_5,
  input  in_6
);

  wire and_1_out, clock_1_out;

  Clock clock_1 (.out(clock_1_out));
  and and_1 (and_1_out, clock_1_out, in_2);
  LED led_1 (.in(and_1_out));
  Hex_Digit_Display hex_digit_display_1 (.value({in_6, in_5, in_4, in_3}));  // open: dp
endmodule
