// Logisim project CPU.circ as structural Verilog: 9 circuits, main circuit CPU
module CPU (
  output [7:0] out_1,
  output [7:0] out_2,
  output [7:0] bus_de_Direccion,
  output [7:0] out_4,
  output [7:0] PC_inmediato,
  output [7:0] out_6,
  output [1:0] AddRSel,
  output [7:0] Datos_Inmediatos,
  output [7:0] DBus,
  output [7:0] dValor,
  output [7:0] ALU_Salida,
  output [7:0] SBus,
  output [1:0] ALUop,
  output PC_Sel,
  output [1:0] Fase,
  output PC__Carga
);

  wire clock_1_out, clock_2_out, clock_3_out, clock_4_out, DEscribe, IMCarga, IrCarga, LeeEscribe,
       registro_de_archivo_1_cero, registro_de_archivo_1_negativo;
  wire [1:0] dRegSel, \Re__Selección , sRegSel;
  wire [7:0] PC_q, register_1_q, Registro_Inmediato_q, undriven;

  RAM #(.bus("separate")) ram_1 (
    .addr(bus_de_Direccion), .din(DBus), .data(Datos_Inmediatos), .str(LeeEscribe), .clk(clock_1_out));  // open: sel, ld, clr
  Clock clock_1 (.out(clock_1_out));
  Multiplexer #(.select(2), .width(8), .enable("false")) multiplexer_1 (
    .in0(PC_q), .in1(Registro_Inmediato_q), .in2(SBus), .in3(DBus), .out(bus_de_Direccion), .sel(AddRSel));
  Register Registro_Inmediato (
    .D(Datos_Inmediatos), .en(IMCarga), .Q(Registro_Inmediato_q), .clk(clock_2_out));  // open: clr
  Clock clock_2 (.out(clock_2_out));
  Register register_1 (.D(Datos_Inmediatos), .en(IrCarga), .Q(register_1_q), .clk(clock_3_out));  // open: clr
  Clock clock_3 (.out(clock_3_out));
  Multiplexer #(.select(2), .width(8), .enable("false")) multiplexer_2 (
    .in0(Registro_Inmediato_q), .in1(SBus), .in2(Datos_Inmediatos), .in3(ALU_Salida), .out(dValor),
    .sel(\Re__Selección ));
  Multiplexer #(.width(8), .enable("false")) multiplexer_3 (
    .in0(Registro_Inmediato_q), .in1(undriven), .out(PC_inmediato), .sel(PC_Sel));
  Unidad_de_Control unidad_de_control_1 (
    .IR_Carga(IrCarga), .IM_Carga(IMCarga), .PC_SELECCION(PC_Sel), .PCLoad(PC__Carga),
    .Leer_y_Escribir(LeeEscribe), .\Reg_Selección (\Re__Selección ), .\Dir_Selección (AddRSel),
    .Escribe(DEscribe), .CERO(registro_de_archivo_1_cero), .IR_value(register_1_q),
    .NEGATIVO(registro_de_archivo_1_negativo), .Op_ALU(ALUop), .SREGSEL(sRegSel), .DREGSEL(dRegSel),
    .Fase(Fase));
  Registro_de_Archivo registro_de_archivo_1 (
    .dEscribe(DEscribe), .De_Valor(dValor), .DBUS(DBus), .NEGATIVO(registro_de_archivo_1_negativo),
    .R1(out_2), .R2(out_4), .R3(out_6), .DREGSEL(dRegSel), .SREGSEL(sRegSel), .SBUS(SBus), .R0(out_1),
    .CERO(registro_de_archivo_1_cero));
  Register PC (.D(PC_inmediato), .en(PC__Carga), .Q(PC_q), .clk(clock_4_out));  // open: clr
  Clock clock_4 (.out(clock_4_out));
  PC_SUMADOR PC_Sumador (.PC_in(undriven), .PC_out(PC_q));
  _8_bit_ALU ALU (.A(DBus), .B(SBus), .Operacion(ALUop), .Resultado(ALU_Salida));

  // Other names for the same wires on the sheet: PC_Carga = PC__Carga; R0[7:0] = out_1; R1[7:0] = out_2;
  //   R2[7:0] = out_4; R3[7:0] = out_6

  // Notes on the sheet:
  //   bus de datos de salida
  //   RAM
  //   DBUS
  //   SBUS
  //   REGISTRO DE VALORES
endmodule

// U. CONTROL
module Unidad_de_Control (
  input  [7:0] IR_value,
  input  CERO,
  input  NEGATIVO,
  output [1:0] Fase,
  output [1:0] DREGSEL,
  output [1:0] SREGSEL,
  output [1:0] Op_ALU,
  output IR_Carga,
  output IM_Carga,
  output PC_SELECCION,
  output PCLoad,
  output Leer_y_Escribir,
  output [1:0] \Reg_Selección ,
  output [1:0] \Dir_Selección ,
  output Escribe
);

  wire and_1_out, and_2_out, and_3_out, and_4_out, and_5_out, clock_1_out, multiplexer_2_out,
       multiplexer_6_out, not_1_out, not_2_out, not_3_out, not_4_out, or_1_out;
  wire [1:0] multiplexer_1_out, multiplexer_11_out;

  not not_1 (not_1_out, CERO);
  not not_2 (not_2_out, NEGATIVO);
  and and_1 (and_1_out, not_1_out, not_2_out);
  Multiplexer #(.select(4), .width(2), .enable("false")) multiplexer_1 (
    .in0(2'b11), .in1(2'b11), .in2(2'b11), .in3(2'b11), .in4(2'b10), .in5(2'b00), .in6(2'b01), .in7(2'b00),
    .in8(2'b00), .in9(2'b00), .in10(2'b00), .in11(2'b00), .in12(2'b10), .in13(2'b00), .in14(2'b00),
    .in15(2'b00), .out(multiplexer_1_out), .sel(IR_value[7:4]));
  not not_3 (not_3_out, IR_value[6]);
  Multiplexer #(.select(2), .enable("false")) multiplexer_2 (
    .in0(CERO), .in1(not_1_out), .in2(and_1_out), .in3(NEGATIVO), .out(multiplexer_2_out), .sel(IR_value[5:4]));
  Multiplexer #(.select(2), .width(2), .enable("false")) multiplexer_3 (
    .in0(2'b00), .in1(2'b00), .in2(multiplexer_1_out), .in3(2'b00), .out(\Reg_Selección ), .sel(Fase));
  Multiplexer #(.select(2), .enable("false")) multiplexer_4 (
    .in0(1'b1), .in1(1'b0), .in2(1'b0), .in3(1'b0), .out(IR_Carga), .sel(Fase));
  and and_2 (and_2_out, not_3_out, IR_value[7], multiplexer_2_out);
  and and_3 (and_3_out, IR_value[4], IR_value[5], IR_value[6], IR_value[7]);
  or or_1 (or_1_out, and_2_out, and_3_out);
  Multiplexer #(.select(2), .enable("false")) multiplexer_5 (
    .in0(1'b1), .in1(IR_value[7]), .in2(or_1_out), .in3(1'b0), .out(PCLoad), .sel(Fase));
  Multiplexer #(.select(4), .enable("false")) multiplexer_6 (
    .in0(1'b1), .in1(1'b1), .in2(1'b1), .in3(1'b1), .in4(1'b1), .in5(1'b1), .in6(1'b0), .in7(1'b0),
    .in8(1'b0), .in9(1'b0), .in10(1'b0), .in11(1'b0), .in12(1'b1), .in13(1'b0), .in14(1'b1), .in15(1'b0),
    .out(multiplexer_6_out), .sel(IR_value[7:4]));
  Multiplexer #(.select(2), .enable("false")) multiplexer_7 (
    .in0(1'b0), .in1(IR_value[7]), .in2(1'b0), .in3(1'b0), .out(IM_Carga), .sel(Fase));
  Multiplexer #(.select(2), .enable("false")) multiplexer_8 (
    .in0(1'b0), .in1(1'b0), .in2(multiplexer_6_out), .in3(1'b0), .out(Escribe), .sel(Fase));
  Counter #(.width(2), .max('h3)) counter_1 (
    .Q(Fase), .clk(clock_1_out), .clr(and_4_out));  // open: load, D, count, carry
  and and_4 (and_4_out, Fase[1], Fase[0]);
  Clock clock_1 (.out(clock_1_out));
  not not_4 (not_4_out, IR_value[5]);
  Multiplexer #(.select(2), .enable("false")) multiplexer_9 (
    .in0(1'b1), .in1(1'b1), .in2(1'b0), .in3(1'b0), .out(PC_SELECCION), .sel(Fase));
  and and_5 (and_5_out, IR_value[4], not_4_out, IR_value[6]);
  Multiplexer #(.select(2), .enable("false")) multiplexer_10 (
    .in0(1'b0), .in1(1'b0), .in2(and_5_out), .in3(1'b0), .out(Leer_y_Escribir), .sel(Fase));
  Multiplexer #(.select(4), .width(2), .enable("false")) multiplexer_11 (
    .in0(2'b00), .in1(2'b00), .in2(2'b00), .in3(2'b00), .in4(2'b10), .in5(2'b10), .in6(2'b00), .in7(2'b00),
    .in8(2'b00), .in9(2'b00), .in10(2'b00), .in11(2'b00), .in12(2'b00), .in13(2'b01), .in14(2'b01),
    .in15(2'b00), .out(multiplexer_11_out), .sel(IR_value[7:4]));
  Multiplexer #(.select(2), .width(2), .enable("false")) multiplexer_12 (
    .in0(2'b00), .in1(2'b00), .in2(multiplexer_11_out), .in3(2'b00), .out(\Dir_Selección ), .sel(Fase));

  assign DREGSEL = IR_value[3:2];
  assign Op_ALU = IR_value[5:4];
  assign SREGSEL = IR_value[1:0];

  // Other names for the same wires on the sheet: irbit4 = IR_value[4]; Op1_Op2[3:0] = IR_value[7:4];
  //   Op2[1:0] = IR_value[5:4]; irbit5 = IR_value[5]; irbit6 = IR_value[6]; Op1[1:0] = IR_value[7:6];
  //   irbit7 = IR_value[7]; RD[1:0] = IR_value[3:2]; RS[1:0] = IR_value[1:0]

  // Notes on the sheet:
  //   Seleccion de Registro
  //   PC Load
  //   IR LOAD
  //   Escribe Registro de Destino
  //   IMMED LOAD
  //   LECTURA Y ESCRITURA
  //   Phase Counter
  //   PC Selección
  //   Direccion de Seleccion
endmodule

// +
module PC_SUMADOR (
  input  [7:0] PC_in,
  output [7:0] PC_out
);

  Adder adder_1 (.a(PC_in), .b(8'h1), .out(PC_out), .cin(1'b0));  // open: cout
endmodule

// REG. ARCHIVOS
module Registro_de_Archivo (
  input  dEscribe,
  input  [1:0] DREGSEL,
  input  [7:0] De_Valor,
  input  [1:0] SREGSEL,
  output [7:0] R0,
  output [7:0] DBUS,
  output [7:0] R1,
  output [7:0] R2,
  output [7:0] R3,
  output [7:0] SBUS,
  output CERO,
  output NEGATIVO
);

  wire clock_1_out, demultiplexer_1_out0, demultiplexer_1_out1, demultiplexer_1_out2, or_1_out;

  Demultiplexer #(.select(2), .enable("false")) demultiplexer_1 (
    .out0(demultiplexer_1_out0), .out1(demultiplexer_1_out1), .out2(demultiplexer_1_out2), .in(dEscribe),
    .sel(DREGSEL));  // open: out3
  Register register_1 (.D(De_Valor), .en(demultiplexer_1_out0), .Q(R0), .clk(clock_1_out));  // open: clr
  Register register_2 (.D(De_Valor), .en(demultiplexer_1_out1), .Q(R1), .clk(clock_1_out));  // open: clr
  Register register_3 (.D(De_Valor), .en(demultiplexer_1_out2), .Q(R2), .clk(clock_1_out));  // open: clr
  Register register_4 (.D(De_Valor), .en(demultiplexer_1_out2), .Q(R3), .clk(clock_1_out));  // open: clr
  Clock clock_1 (.out(clock_1_out));
  Multiplexer #(.select(2), .width(8), .enable("false")) multiplexer_1 (
    .in0(R0), .in1(R1), .in2(R2), .in3(R3), .out(DBUS), .sel(DREGSEL));
  Multiplexer #(.select(2), .width(8), .enable("false")) multiplexer_2 (
    .in0(R0), .in1(R1), .in2(R2), .in3(R3), .out(SBUS), .sel(SREGSEL));
  or or_1 (or_1_out, DBUS[0], DBUS[1], DBUS[2], DBUS[3], DBUS[4], DBUS[5], DBUS[6], DBUS[7]);
  not not_1 (CERO, or_1_out);

  assign NEGATIVO = DBUS[7];

  // Other names for the same wires on the sheet: DRS[1:0] = DREGSEL
endmodule

// AND
module _8_bit_AND (
  input  [7:0] A,
  input  [7:0] B,
  output [7:0] Resultado
);

  and AND (Resultado[0], A[0], B[0]);
  and AND_2 (Resultado[1], A[1], B[1]);
  and AND_3 (Resultado[2], A[2], B[2]);
  and AND_4 (Resultado[3], A[3], B[3]);
  and AND_5 (Resultado[4], A[4], B[4]);
  and AND_6 (Resultado[5], A[5], B[5]);
  and AND_7 (Resultado[6], A[6], B[6]);
  and AND_8 (Resultado[7], A[7], B[7]);
endmodule

// OR
module _8_bit_OR (
  input  [7:0] A,
  input  [7:0] B,
  output [7:0] Resultado
);

  or OR (Resultado[0], A[0], B[0]);
  or OR_2 (Resultado[1], A[1], B[1]);
  or OR_3 (Resultado[2], A[2], B[2]);
  or OR_4 (Resultado[3], A[3], B[3]);
  or OR_5 (Resultado[4], A[4], B[4]);
  or OR_6 (Resultado[5], A[5], B[5]);
  or OR_7 (Resultado[6], A[6], B[6]);
  or OR_8 (Resultado[7], A[7], B[7]);
endmodule

// +
module _1_bit_adicion (
  input  Carril_de_etrada,
  input  A,
  input  B,
  output Resultado,
  output Carril_de_Salida
);

  wire AND_2_out, AND_out, XOR_out;

  and AND (AND_out, A, B);
  xor XOR (XOR_out, A, B);
  or OR (Carril_de_Salida, AND_out, AND_2_out);
  and AND_2 (AND_2_out, Carril_de_etrada, XOR_out);
  xor XOR_2 (Resultado, Carril_de_etrada, XOR_out);
endmodule

// +/-
module _8_bit_Suma_Resta (
  input  Control,
  input  [7:0] A,
  input  [7:0] B,
  output [7:0] Resultado
);

  wire n1_bit_adicion_1_carril_de_salida, n1_bit_adicion_2_carril_de_salida,
       n1_bit_adicion_3_carril_de_salida, n1_bit_adicion_4_carril_de_salida,
       n1_bit_adicion_5_carril_de_salida, n1_bit_adicion_6_carril_de_salida,
       n1_bit_adicion_7_carril_de_salida, XOR_2_out, XOR_3_out, XOR_4_out, XOR_5_out, XOR_6_out, XOR_7_out,
       XOR_8_out, XOR_out;

  xor XOR (XOR_out, Control, B[0]);
  xor XOR_2 (XOR_2_out, Control, B[1]);
  xor XOR_3 (XOR_3_out, Control, B[2]);
  xor XOR_4 (XOR_4_out, Control, B[3]);
  xor XOR_5 (XOR_5_out, Control, B[4]);
  xor XOR_6 (XOR_6_out, Control, B[5]);
  xor XOR_7 (XOR_7_out, Control, B[6]);
  xor XOR_8 (XOR_8_out, Control, B[7]);
  _1_bit_adicion u_1_bit_adicion_1 (
    .A(A[0]), .B(XOR_out), .Carril_de_etrada(Control), .Carril_de_Salida(n1_bit_adicion_1_carril_de_salida),
    .Resultado(Resultado[0]));
  _1_bit_adicion u_1_bit_adicion_2 (
    .A(A[1]), .B(XOR_2_out), .Carril_de_etrada(n1_bit_adicion_1_carril_de_salida),
    .Carril_de_Salida(n1_bit_adicion_2_carril_de_salida), .Resultado(Resultado[1]));
  _1_bit_adicion u_1_bit_adicion_3 (
    .A(A[2]), .B(XOR_3_out), .Carril_de_etrada(n1_bit_adicion_2_carril_de_salida),
    .Carril_de_Salida(n1_bit_adicion_3_carril_de_salida), .Resultado(Resultado[2]));
  _1_bit_adicion u_1_bit_adicion_4 (
    .A(A[3]), .B(XOR_4_out), .Carril_de_etrada(n1_bit_adicion_3_carril_de_salida),
    .Carril_de_Salida(n1_bit_adicion_4_carril_de_salida), .Resultado(Resultado[3]));
  _1_bit_adicion u_1_bit_adicion_5 (
    .A(A[4]), .B(XOR_5_out), .Carril_de_etrada(n1_bit_adicion_4_carril_de_salida),
    .Carril_de_Salida(n1_bit_adicion_5_carril_de_salida), .Resultado(Resultado[4]));
  _1_bit_adicion u_1_bit_adicion_6 (
    .A(A[5]), .B(XOR_6_out), .Carril_de_etrada(n1_bit_adicion_5_carril_de_salida),
    .Carril_de_Salida(n1_bit_adicion_6_carril_de_salida), .Resultado(Resultado[5]));
  _1_bit_adicion u_1_bit_adicion_7 (
    .A(A[6]), .B(XOR_7_out), .Carril_de_etrada(n1_bit_adicion_6_carril_de_salida),
    .Carril_de_Salida(n1_bit_adicion_7_carril_de_salida), .Resultado(Resultado[6]));
  _1_bit_adicion u_1_bit_adicion_8 (
    .A(A[7]), .B(XOR_8_out), .Carril_de_etrada(n1_bit_adicion_7_carril_de_salida), .Resultado(Resultado[7]));  // open: Carril_de_Salida
endmodule

module _8_bit_ALU (
  input  [7:0] A,
  input  [7:0] B,
  input  [1:0] Operacion,
  output [7:0] Resultado
);

  wire [7:0] multiplexer_1_out, n8_bit_and_1_resultado, n8_bit_or_1_resultado, n8_bit_suma_resta_1_resultado;

  _8_bit_AND u_8_bit_and_1 (.B(B), .Resultado(n8_bit_and_1_resultado), .A(A));
  _8_bit_OR u_8_bit_or_1 (.B(B), .Resultado(n8_bit_or_1_resultado), .A(A));
  _8_bit_Suma_Resta u_8_bit_suma_resta_1 (
    .Control(Operacion[1]), .B(B), .Resultado(n8_bit_suma_resta_1_resultado), .A(A));
  Multiplexer #(.width(8), .enable("false")) multiplexer_1 (
    .in0(n8_bit_and_1_resultado), .in1(n8_bit_or_1_resultado), .out(multiplexer_1_out), .sel(Operacion[1]));
  Multiplexer #(.width(8), .enable("false")) multiplexer_2 (
    .in0(multiplexer_1_out), .in1(n8_bit_suma_resta_1_resultado), .out(Resultado), .sel(Operacion[0]));
endmodule
