// Logisim project 10señales.circ as structural Verilog: 1 circuit, main circuit main
module main (
  input  in_1,
  input  in_2,
  output out_3
);

  wire not_1_out, or_1_out;

  buf or_1 (or_1_out, in_2);  // OR_Gate
  not not_1 (not_1_out, or_1_out);
  and and_1 (out_3, in_1, 1'b1, not_1_out);
endmodule
