// Logisim project ALU.circ as structural Verilog: 1 circuit, main circuit main
module main (
  input  [7:0] Operando1,
  input  [7:0] Operando2,
  input  S1,
  input  S2,
  input  in_5,
  input  in_6,
  input  in_7,
  output [7:0] out_8,
  output [7:0] Resultado
);

  wire adder_1_cout, and_1_out, and_2_out, and_3_out, and_4_out, controlled_buffer_1_out, not_1_out,
       not_2_out, not_3_out, not_4_out, not_5_out, not_8_out, or_2_p10;
  wire [7:0] adder_1_out, adder_2_out, and_5_out, not_6_out, not_7_out, or_1_out;
  wire [7:1] and_6_out;

  not not_1 (not_1_out, S2);
  not not_2 (not_2_out, S1);
  not not_3 (not_3_out, S1);
  not not_4 (not_4_out, S2);
  and and_1 (and_1_out, not_1_out, not_2_out, not_5_out);
  not not_5 (not_5_out, in_7);
  and and_2 (and_2_out, S2, not_3_out);
  and and_3 (and_3_out, not_4_out, S1);
  and and_4 (and_4_out, S2, S1);
  assign not_6_out = ~{8{1'b1}};  // NOT_Gate not_6, 8 bits wide
  assign not_7_out = ~{8{1'b1}};  // NOT_Gate not_7, 8 bits wide
  Adder #(.width(8)) adder_1 (.a(Operando1), .b(Operando2), .out(adder_1_out), .cout(adder_1_cout));  // open: cin
  assign controlled_buffer_1_out = and_1_out ? adder_1_cout : 1'bz;  // Controlled_Buffer controlled_buffer_1
  assign and_5_out = Operando2 & Operando1;  // AND_Gate and_5, 8 bits wide
  not not_8 (not_8_out, 1'b1);
  assign or_1_out = Operando2 | Operando1 | not_6_out;  // OR_Gate or_1, 8 bits wide
  assign Resultado = and_4_out ? ~Operando1 : 8'bz;  // Controlled_Inverter controlled_inverter_1
  Adder #(.width(8)) adder_2 (.a(Operando1), .b(not_7_out), .out(adder_2_out));  // open: cin, cout
  assign Resultado = and_1_out ? adder_1_out : 8'bz;  // Controlled_Buffer controlled_buffer_2
  assign Resultado = and_2_out ? and_5_out : 8'bz;  // Controlled_Buffer controlled_buffer_3
  and and_6 (and_6_out[1], Resultado[7], in_6);
  assign Resultado = and_3_out ? or_1_out : 8'bz;  // Controlled_Buffer controlled_buffer_4
  assign Resultado = in_7 ? adder_2_out : 8'bz;  // Controlled_Buffer controlled_buffer_5
  // OR_Gate #(.width(1)) or_2: pin names not known; wires that end beside it: Resultado[0], Resultado[1], Resultado[2], Resultado[3], Resultado[5], Resultado[6], Resultado[7], not_8_out, Resultado[4], or_2_p10
  or or_3 (and_6_out[7], 1'b0, 1'b0, 1'b0, controlled_buffer_1_out, 1'b0);
  not not_9 (and_6_out[3], or_2_p10);
  not not_10 (and_6_out[6], 1'b1);
  Register #(.width(8)) register_1 (
    .D({and_6_out[7:6], and_6_out[7:6], and_6_out[3], and_6_out[6], and_6_out[1], and_6_out[6]}), .Q(out_8),
    .clk(in_5));  // open: en, clr

  // Notes on the sheet:
  //   Carry
  //   Desborde
  //   Zero
  //   Negativo
endmodule
