// Logisim project Copia de Registro.circ as structural Verilog: 3 circuits, main circuit Registro8
module Registro8 (
  input  in_1,
  input  in_2,
  input  in_3,
  input  in_4,
  input  in_5,
  input  in_6,
  input  in_7,
  input  in_8,
  input  in_9
);

  wire and_1_out, clock_1_out, d_ff_1_q, d_ff_2_q, d_ff_3_q, d_ff_4_q, d_ff_5_q, d_ff_6_q, d_ff_7_q, d_ff_8_q;

  Clock #(.highDuration(1), .lowDuration(1)) clock_1 (.out(clock_1_out));
  and and_1 (and_1_out, clock_1_out, in_1);
  D_Flip_Flop d_ff_1 (.clk(and_1_out), .D(in_2), .Q(d_ff_1_q));  // open: Qn, preset, en, reset
  D_Flip_Flop d_ff_2 (.clk(and_1_out), .D(in_4), .Q(d_ff_2_q));  // open: Qn, preset, en, reset
  D_Flip_Flop d_ff_3 (.clk(and_1_out), .D(in_3), .Q(d_ff_3_q));  // open: Qn, preset, en, reset
  D_Flip_Flop d_ff_4 (.clk(and_1_out), .D(in_5), .Q(d_ff_4_q));  // open: Qn, preset, en, reset
  D_Flip_Flop d_ff_5 (.clk(and_1_out), .D(in_6), .Q(d_ff_5_q));  // open: Qn, preset, en, reset
  D_Flip_Flop d_ff_6 (.clk(and_1_out), .D(in_7), .Q(d_ff_6_q));  // open: Qn, preset, en, reset
  D_Flip_Flop d_ff_7 (.clk(and_1_out), .D(in_8), .Q(d_ff_7_q));  // open: Qn, preset, en, reset
  D_Flip_Flop d_ff_8 (.clk(and_1_out), .D(in_9), .Q(d_ff_8_q));  // open: Qn, preset, en, reset
endmodule

module Sumador1bit (
  input  in_1,
  input  in_2,
  output out_3,
  output out_4
);

  and and_1 (out_4, in_1, in_2);
  xor xor_1 (out_3, in_1, in_2);
endmodule

module Sumador2Bits (
  input  in_1,
  input  in_2,
  input  in_3,
  input  in_4,
  output out_5,
  output out_6,
  output out_7
);

  wire sumador1bit_1_out_4, sumador1bit_2_out_3, sumador1bit_2_out_4;

  Sumador1bit sumador1bit_1 (.in_1(in_2), .in_2(in_4), .out_3(out_5), .out_4(sumador1bit_1_out_4));
  Sumador1bit sumador1bit_2 (
    .in_1(sumador1bit_1_out_4), .in_2(in_1), .out_3(sumador1bit_2_out_3), .out_4(sumador1bit_2_out_4));
  Sumador1bit sumador1bit_3 (.in_1(sumador1bit_2_out_3), .in_2(in_3), .out_3(out_6), .out_4(out_7));
endmodule
