// Logisim project Copia de alu_secundaria.circ as structural Verilog: 1 circuit, main circuit main
module main (
  input  [6:0] ALU_Secundaria,
  output [6:0] out_2
);

  wire [6:6] not_1_out;

  not not_1 (not_1_out[6], 1'b1);
  Adder #(.width(7)) adder_1 (
    .a(ALU_Secundaria), .b({{3{not_1_out[6]}}, 2'b11, {2{not_1_out[6]}}}), .out(out_2));  // open: cin, cout
endmodule
