// Logisim project Copia de registros.circ as structural Verilog: 1 circuit, main circuit main
module main (
  input  [7:0] in_1,
  input  [3:0] in_2,
  input  in_3,
  input  in_4,
  output [7:0] out_5
);

  wire controlled_buffer_2_out, controlled_buffer_3_out, controlled_buffer_4_out, controlled_buffer_5_out,
       controlled_buffer_6_out, controlled_buffer_7_out, controlled_buffer_8_out, controlled_buffer_9_out,
       controlled_buffer_10_out, controlled_buffer_11_out, controlled_buffer_12_out,
       controlled_buffer_13_out, controlled_buffer_14_out, controlled_buffer_15_out,
       controlled_buffer_16_out, controlled_buffer_17_out, decoder_1_out0, decoder_1_out1, decoder_1_out2,
       decoder_1_out3, decoder_1_out4, decoder_1_out5, decoder_1_out6, decoder_1_out7, decoder_1_out8,
       decoder_1_out9, decoder_1_out10, decoder_1_out11, decoder_1_out12, decoder_1_out13, decoder_1_out14,
       decoder_1_out15;
  wire [3:0] controlled_buffer_1_out;
  wire [7:0] register_2_q, register_3_q, register_4_q, register_5_q, register_6_q, register_7_q,
       register_8_q, register_9_q, register_10_q, register_11_q, register_12_q, register_13_q, register_14_q,
       register_15_q, register_16_q;

  Decoder #(.select(4), .tristate("false")) decoder_1 (
    .out0(decoder_1_out0), .out1(decoder_1_out1), .out2(decoder_1_out2), .out3(decoder_1_out3),
    .out4(decoder_1_out4), .out5(decoder_1_out5), .out6(decoder_1_out6), .out7(decoder_1_out7),
    .out8(decoder_1_out8), .out9(decoder_1_out9), .out10(decoder_1_out10), .out11(decoder_1_out11),
    .out12(decoder_1_out12), .out13(decoder_1_out13), .out14(decoder_1_out14), .out15(decoder_1_out15),
    .sel(controlled_buffer_1_out));
  assign controlled_buffer_1_out = in_3 ? in_2 : 4'bz;  // Controlled_Buffer controlled_buffer_1
  Register #(.width(8)) register_1 (.D(in_1), .Q(out_5), .clk(controlled_buffer_2_out));  // open: en, clr
  assign controlled_buffer_2_out = in_4 ? decoder_1_out0 : 1'bz;  // Controlled_Buffer controlled_buffer_2
  assign controlled_buffer_3_out = in_4 ? decoder_1_out1 : 1'bz;  // Controlled_Buffer controlled_buffer_3
  assign controlled_buffer_4_out = in_4 ? decoder_1_out2 : 1'bz;  // Controlled_Buffer controlled_buffer_4
  assign controlled_buffer_5_out = in_4 ? decoder_1_out3 : 1'bz;  // Controlled_Buffer controlled_buffer_5
  assign controlled_buffer_6_out = in_4 ? decoder_1_out4 : 1'bz;  // Controlled_Buffer controlled_buffer_6
  assign controlled_buffer_7_out = in_4 ? decoder_1_out5 : 1'bz;  // Controlled_Buffer controlled_buffer_7
  assign controlled_buffer_8_out = in_4 ? decoder_1_out6 : 1'bz;  // Controlled_Buffer controlled_buffer_8
  assign controlled_buffer_9_out = in_4 ? decoder_1_out7 : 1'bz;  // Controlled_Buffer controlled_buffer_9
  assign controlled_buffer_10_out = in_4 ? decoder_1_out8 : 1'bz;  // Controlled_Buffer controlled_buffer_10
  assign controlled_buffer_11_out = in_4 ? decoder_1_out9 : 1'bz;  // Controlled_Buffer controlled_buffer_11
  assign controlled_buffer_12_out = in_4 ? decoder_1_out10 : 1'bz;  // Controlled_Buffer controlled_buffer_12
  assign controlled_buffer_13_out = in_4 ? decoder_1_out11 : 1'bz;  // Controlled_Buffer controlled_buffer_13
  assign controlled_buffer_14_out = in_4 ? decoder_1_out12 : 1'bz;  // Controlled_Buffer controlled_buffer_14
  assign controlled_buffer_15_out = in_4 ? decoder_1_out13 : 1'bz;  // Controlled_Buffer controlled_buffer_15
  assign controlled_buffer_16_out = in_4 ? decoder_1_out14 : 1'bz;  // Controlled_Buffer controlled_buffer_16
  assign controlled_buffer_17_out = in_4 ? decoder_1_out15 : 1'bz;  // Controlled_Buffer controlled_buffer_17
  Register #(.width(8)) register_2 (.D(in_1), .Q(register_2_q), .clk(controlled_buffer_3_out));  // open: en, clr
  Register #(.width(8)) register_3 (.D(in_1), .Q(register_3_q), .clk(controlled_buffer_4_out));  // open: en, clr
  Register #(.width(8)) register_4 (.D(in_1), .Q(register_4_q), .clk(controlled_buffer_5_out));  // open: en, clr
  Register #(.width(8)) register_5 (.D(in_1), .Q(register_5_q), .clk(controlled_buffer_6_out));  // open: en, clr
  Register #(.width(8)) register_6 (.D(in_1), .Q(register_6_q), .clk(controlled_buffer_7_out));  // open: en, clr
  Register #(.width(8)) register_7 (.D(in_1), .Q(register_7_q), .clk(controlled_buffer_8_out));  // open: en, clr
  Register #(.width(8)) register_8 (.D(in_1), .Q(register_8_q), .clk(controlled_buffer_9_out));  // open: en, clr
  Register #(.width(8)) register_9 (.D(in_1), .Q(register_9_q), .clk(controlled_buffer_10_out));  // open: en, clr
  Register #(.width(8)) register_10 (.D(in_1), .Q(register_10_q), .clk(controlled_buffer_11_out));  // open: en, clr
  Register #(.width(8)) register_11 (.D(in_1), .Q(register_11_q), .clk(controlled_buffer_12_out));  // open: en, clr
  Register #(.width(8)) register_12 (.D(in_1), .Q(register_12_q), .clk(controlled_buffer_13_out));  // open: en, clr
  Register #(.width(8)) register_13 (.D(in_1), .Q(register_13_q), .clk(controlled_buffer_14_out));  // open: en, clr
  Register #(.width(8)) register_14 (.D(in_1), .Q(register_14_q), .clk(controlled_buffer_15_out));  // open: en, clr
  Register #(.width(8)) register_15 (.D(in_1), .Q(register_15_q), .clk(controlled_buffer_16_out));  // open: en, clr
  Register #(.width(8)) register_16 (.D(in_1), .Q(register_16_q), .clk(controlled_buffer_17_out));  // open: en, clr
endmodule
