// Logisim project Unidadcontrol.circ as structural Verilog: 1 circuit, main circuit main
module main (
  input  [4:0] in_1,
  input  in_2,
  input  in_3,
  input  n,
  input  z,
  input  d,
  input  c,
  output out_8,
  output s2,
  output s1,
  output out_11,
  output out_12,
  output out_13,
  output out_14,
  output out_15,
  output out_16,
  output out_17,
  output out_18,
  output out_19,
  output out_20,
  output out_21,
  output out_22,
  output out_23,
  output out_24,
  output out_25,
  output out_26,
  output out_27,
  output out_28,
  output out_29,
  output [1:0] out_30
);

  wire and_1_out, and_2_out, and_3_out, and_4_out, and_5_out, and_6_out, and_7_out, and_8_out, and_9_out,
       and_10_out, and_11_out, and_12_out, and_13_out, and_14_out, and_15_out, and_16_out, and_17_out,
       and_18_out, controlled_buffer_5_out, d_ff_1_q, d_ff_2_q, d_ff_3_q, d_ff_4_q, d_ff_5_q, d_ff_6_q,
       d_ff_7_q, d_ff_8_q, d_ff_9_q, d_ff_10_q, d_ff_11_q, d_ff_12_q, d_ff_13_q, d_ff_14_q, d_ff_15_q,
       d_ff_16_q, d_ff_19_q, decoder_1_out0, decoder_1_out1, decoder_1_out2, decoder_1_out3, decoder_1_out4,
       decoder_1_out5, decoder_1_out6, decoder_1_out7, decoder_1_out8, decoder_1_out9, decoder_1_out10,
       decoder_1_out15, main_1_p1, main_1_p2, main_2_inc_pc, main_2_out_14, main_2_out_16, main_2_out_17,
       main_2_out_18, main_2_out_19, main_2_out_20, main_2_out_21, main_2_out_22, main_2_out_23,
       main_2_out_24, main_2_out_25, main_2_out_26, main_2_out_27, main_2_out_28, main_2_out_29,
       main_2_out_30, main_2_out_31, main_2_out_32, not_1_out, not_2_out, not_3_out, not_4_out, not_5_out,
       not_6_out, not_7_out, not_8_out, or_1_out, or_2_out, or_3_out, or_4_out, or_5_out, or_6_out, or_8_out,
       or_9_out, undriven;

  or or_1 (or_1_out, main_2_out_14, d_ff_3_q);
  D_Flip_Flop d_ff_1 (.clk(in_3), .D(d_ff_2_q), .Q(d_ff_1_q), .reset(or_1_out));  // open: Qn, preset, en
  D_Flip_Flop d_ff_2 (.clk(in_3), .D(in_2), .Q(d_ff_2_q), .reset(main_2_out_14));  // open: Qn, preset, en
  // _10señales_main main_1: pin names not known; wires that end beside it: main_1_p1, main_1_p2
  or or_2 (or_2_out, d_ff_3_q, main_1_p2);
  or or_3 (or_3_out, decoder_1_out0, decoder_1_out1);
  D_Flip_Flop d_ff_3 (.clk(in_3), .D(or_2_out), .Q(d_ff_3_q), .reset(main_2_out_14));  // open: Qn, preset, en
  not not_1 (not_1_out, in_1[0]);
  not not_2 (not_2_out, in_1[0]);
  or or_4 (or_4_out, decoder_1_out4, controlled_buffer_5_out);
  and and_1 (and_1_out, d_ff_3_q, decoder_1_out7, not_3_out);
  not not_3 (not_3_out, in_1[0]);
  and and_2 (and_2_out, d_ff_3_q, decoder_1_out7, in_1[0]);
  and and_3 (and_3_out, decoder_1_out8, d_ff_3_q, not_4_out);
  not not_4 (not_4_out, in_1[0]);
  and and_4 (and_4_out, decoder_1_out8, d_ff_3_q, in_1[0]);
  and and_5 (and_5_out, decoder_1_out10, d_ff_3_q);
  and and_6 (and_6_out, decoder_1_out15, d_ff_3_q);
  and and_7 (and_7_out, d_ff_3_q, or_3_out);
  and and_8 (and_8_out, d_ff_3_q, decoder_1_out5);
  and and_9 (and_9_out, d_ff_3_q, decoder_1_out9);
  and and_10 (and_10_out, d_ff_3_q, decoder_1_out6);
  and and_11 (and_11_out, d_ff_3_q, decoder_1_out2, not_1_out);
  and and_12 (and_12_out, decoder_1_out2, in_1[0], d_ff_3_q);
  and and_13 (and_13_out, decoder_1_out3, d_ff_3_q, not_2_out);
  and and_14 (and_14_out, decoder_1_out3, d_ff_3_q, in_1[0]);
  D_Flip_Flop d_ff_4 (.clk(in_3), .D(and_7_out), .Q(d_ff_4_q), .reset(main_2_out_14));  // open: Qn, preset, en
  D_Flip_Flop d_ff_5 (.clk(in_3), .D(and_8_out), .Q(d_ff_5_q), .reset(main_2_out_14));  // open: Qn, preset, en
  D_Flip_Flop d_ff_6 (.clk(in_3), .D(and_9_out), .Q(d_ff_6_q), .reset(main_2_out_14));  // open: Qn, preset, en
  D_Flip_Flop d_ff_7 (.clk(in_3), .D(and_10_out), .Q(d_ff_7_q), .reset(main_2_out_14));  // open: Qn, preset, en
  D_Flip_Flop d_ff_8 (.clk(in_3), .D(and_11_out), .Q(d_ff_8_q), .reset(main_2_out_14));  // open: Qn, preset, en
  D_Flip_Flop d_ff_9 (.clk(in_3), .D(and_12_out), .Q(d_ff_9_q), .reset(main_2_out_14));  // open: Qn, preset, en
  D_Flip_Flop d_ff_10 (.clk(in_3), .D(and_13_out), .Q(d_ff_10_q), .reset(main_2_out_14));  // open: Qn, preset, en
  D_Flip_Flop d_ff_11 (.clk(in_3), .D(and_14_out), .Q(d_ff_11_q), .reset(main_2_out_14));  // open: Qn, preset, en
  D_Flip_Flop d_ff_12 (.clk(in_3), .D(or_4_out), .Q(d_ff_12_q), .reset(main_2_out_14));  // open: Qn, preset, en
  D_Flip_Flop d_ff_13 (.clk(in_3), .D(and_1_out), .Q(d_ff_13_q), .reset(main_2_out_14));  // open: Qn, preset, en
  D_Flip_Flop d_ff_14 (.clk(in_3), .D(and_2_out), .Q(d_ff_14_q), .reset(main_2_out_14));  // open: Qn, preset, en
  D_Flip_Flop d_ff_15 (.clk(in_3), .D(and_3_out), .Q(d_ff_15_q), .reset(main_2_out_14));  // open: Qn, preset, en
  D_Flip_Flop d_ff_16 (.clk(in_3), .D(and_4_out), .Q(d_ff_16_q), .reset(main_2_out_14));  // open: Qn, preset, en
  D_Flip_Flop d_ff_17 (.clk(in_3), .D(and_5_out), .Q(out_20), .reset(main_2_out_14));  // open: Qn, preset, en
  D_Flip_Flop d_ff_18 (.clk(in_3), .D(and_6_out), .Q(out_22));  // open: Qn, preset, en, reset
  or or_5 (or_5_out, undriven, and_7_out);
  or or_6 (or_6_out, d_ff_4_q, undriven);
  assign s1 = d_ff_5_q ? d_ff_5_q : 1'bz;  // Controlled_Buffer controlled_buffer_1
  assign s2 = d_ff_5_q ? ~d_ff_5_q : 1'bz;  // Controlled_Inverter controlled_inverter_1
  assign s2 = and_9_out ? d_ff_6_q : 1'bz;  // Controlled_Buffer controlled_buffer_2
  assign s1 = and_9_out ? d_ff_6_q : 1'bz;  // Controlled_Buffer controlled_buffer_3
  assign s2 = d_ff_7_q ? d_ff_7_q : 1'bz;  // Controlled_Buffer controlled_buffer_4
  assign s1 = d_ff_7_q ? ~d_ff_7_q : 1'bz;  // Controlled_Inverter controlled_inverter_2
  assign controlled_buffer_5_out = c ? d_ff_8_q : 1'bz;  // Controlled_Buffer controlled_buffer_5
  assign controlled_buffer_5_out = d ? d_ff_9_q : 1'bz;  // Controlled_Buffer controlled_buffer_6
  assign controlled_buffer_5_out = z ? d_ff_10_q : 1'bz;  // Controlled_Buffer controlled_buffer_7
  assign controlled_buffer_5_out = n ? d_ff_11_q : 1'bz;  // Controlled_Buffer controlled_buffer_8
  Decoder #(.select(4), .tristate("false")) decoder_1 (
    .out0(decoder_1_out0), .out1(decoder_1_out1), .out2(decoder_1_out2), .out3(decoder_1_out3),
    .out4(decoder_1_out4), .out5(decoder_1_out5), .out6(decoder_1_out6), .out7(decoder_1_out7),
    .out8(decoder_1_out8), .out9(decoder_1_out9), .out10(decoder_1_out10), .out15(decoder_1_out15),
    .sel(in_1[4:1]));  // open: out11, out12, out13, out14
  assign s2 = or_5_out ? ~or_6_out : 1'bz;  // Controlled_Inverter controlled_inverter_3
  assign s1 = or_5_out ? ~or_6_out : 1'bz;  // Controlled_Inverter controlled_inverter_4
  or or_7 (out_8, decoder_1_out1, decoder_1_out5, decoder_1_out6);
  not not_5 (not_5_out, c);
  not not_6 (not_6_out, d);
  not not_7 (not_7_out, z);
  not not_8 (not_8_out, n);
  and and_15 (and_15_out, d_ff_8_q, not_5_out);
  and and_16 (and_16_out, d_ff_9_q, not_6_out);
  and and_17 (and_17_out, not_7_out, d_ff_10_q);
  and and_18 (and_18_out, d_ff_11_q, not_8_out);
  or or_8 (or_8_out, main_2_inc_pc, and_15_out, and_16_out, and_17_out, and_18_out);
  D_Flip_Flop d_ff_19 (.clk(in_3), .D(or_8_out), .Q(d_ff_19_q), .reset(main_2_out_14));  // open: Qn, preset, en
  or or_9 (or_9_out, or_6_out, d_ff_5_q, d_ff_7_q);
  secuencias_main main_2 (
    .reloj(in_3), .in_3(or_9_out), .in_4(d_ff_6_q), .in_5(d_ff_12_q), .in_6(d_ff_13_q), .in_7(d_ff_14_q),
    .in_8(d_ff_15_q), .in_9(d_ff_16_q), .in_10(out_20), .in_11(d_ff_1_q), .in_12(d_ff_19_q),
    .in_2(main_2_out_14), .out_16(main_2_out_16), .out_17(main_2_out_17), .out_18(main_2_out_18),
    .out_19(main_2_out_19), .out_20(main_2_out_20), .out_21(main_2_out_21), .out_22(main_2_out_22),
    .out_23(main_2_out_23), .out_24(main_2_out_24), .out_25(main_2_out_25), .out_26(main_2_out_26),
    .out_27(main_2_out_27), .out_28(main_2_out_28), .out_29(main_2_out_29), .out_30(main_2_out_30),
    .out_31(main_2_out_31), .out_32(main_2_out_32), .out_33(out_30), .inc_pc(main_2_inc_pc),
    .out_14(main_2_out_14), .out_15(main_1_p1));
  buf or_10 (out_11, main_2_out_16);  // OR_Gate
  buf or_11 (out_12, main_2_out_17);  // OR_Gate
  buf or_12 (out_13, main_2_out_18);  // OR_Gate
  buf or_13 (out_14, main_2_out_19);  // OR_Gate
  buf or_14 (out_15, main_2_out_20);  // OR_Gate
  buf or_15 (out_16, main_2_out_21);  // OR_Gate
  buf or_16 (out_17, main_2_out_22);  // OR_Gate
  buf or_17 (out_18, main_2_out_23);  // OR_Gate
  buf or_18 (out_19, main_2_out_24);  // OR_Gate
  buf or_19 (out_21, main_2_out_25);  // OR_Gate
  buf or_20 (out_23, main_2_out_26);  // OR_Gate
  buf or_21 (out_24, main_2_out_27);  // OR_Gate
  buf or_22 (out_25, main_2_out_28);  // OR_Gate
  buf or_23 (out_26, main_2_out_29);  // OR_Gate
  buf or_24 (out_27, main_2_out_30);  // OR_Gate
  buf or_25 (out_28, main_2_out_31);  // OR_Gate
  buf or_26 (out_29, main_2_out_32);  // OR_Gate

  // Notes on the sheet:
  //   0
  //   1
  //   2 Suma
  //   8 YLog
  //   14  Invertir
  //   9 OLog
  //   3 Carry
  //   5 Desbor
  //   6Zero
  //   7Neg
  //   4 Salto
  //   10 cargar
  //   11 Guardar
  //   12 Invocar
  //   13 retorne
  //   15 Mover
  //   hlt
  //   reloj
  //   Guardar PC actual en e11 y se le pasa la direccion de IR
  //   se pasa e11 a Pc 
  //   Pasar r1->r2
  //   flipflops = 0
  //   Salida Permitir direrccion de IR en MUX_PC 
  //   Salida Cargar de la direccion del IR al registro
  //   Guarda en la direccion del IR el contenido de e14
  //   Salidas ALU
  //   16 incrementar pc
endmodule
