// Logisim project conversorMemoria_registro.circ as structural Verilog: 1 circuit, main circuit main
module main (
  input  [11:0] in_1,
  output [7:0] out_2
);


  assign out_2 = in_1[7:0];
endmodule
