// Logisim project conversorRegistro_Memoria.circ as structural Verilog: 1 circuit, main circuit main
module main (
  input  [7:0] in_1,
  output [11:0] out_2
);

  not not_1 (out_2[8], 1'b1);
  not not_2 (out_2[9], 1'b1);
  not not_3 (out_2[10], 1'b1);
  not not_4 (out_2[11], 1'b1);

  assign out_2[7:0] = in_1;
endmodule
