// Logisim project decodificadorIR_Memoria.circ as structural Verilog: 1 circuit, main circuit main
module main (
  input  [11:0] in_1,
  output [6:0] Direccion,
  output [3:0] R2,
  output [3:0] R1,
  output [4:0] out_5
);


  assign Direccion = in_1[6:0];
  assign out_5 = in_1[11:7];
  assign R1 = in_1[7:4];
  assign R2 = in_1[3:0];

  // Notes on the sheet:
  //   Entrada IR
  //   Decodificardor IR_Memoria 
  //   CodigoInstruccion
endmodule
