// Logisim project flags.circ as structural Verilog: 1 circuit, main circuit main
module main (
  input  [7:0] Entrada,
  input  Selector,
  output N,
  output Z,
  output D,
  output C
);

  wire [6:0] register_1_q;

  Register #(.width(8)) register_1 (
    .D(Entrada), .Q({C, register_1_q[6], D, register_1_q[4], Z, register_1_q[2], N, register_1_q[0]}),
    .clk(Selector));  // open: en, clr
endmodule
