// Logisim project ir.circ as structural Verilog: 1 circuit, main circuit main
module main (
  input  [11:0] in_1,
  input  in_2,
  output [11:0] out_3
);

  Register #(.width(12)) register_1 (.D(in_1), .Q(out_3), .clk(in_2));  // open: en, clr

  // Notes on the sheet:
  //   IR
endmodule
