// Logisim project main.circ as structural Verilog: 1 circuit, main circuit main
module main (
  input  in_1,
  input  in_2,
  input  [7:0] in_3,
  input  [7:0] in_4,
  input  in_5,
  input  [6:0] in_6,
  input  in_7,
  input  in_8,
  output out_9,
  output [7:0] out_10,
  output out_11,
  output out_12,
  output [7:0] out_13,
  output out_14,
  output [6:0] PC,
  output [6:0] out_16
);

  wire [6:0] multiplexer_1_out;

  ALU_main main_1 (
    .S1(in_1), .S2(in_2), .Operando1(in_3), .Operando2(in_4), .out_8(out_10), .Resultado(out_13));  // open: in_7, in_6, in_5
  pc_main main_2 (.in_1(multiplexer_1_out), .in_2(in_7), .out_3(PC));
  flags_main main_3 (.Entrada(out_10), .Selector(in_5), .N(out_9), .Z(out_11), .D(out_12), .C(out_14));
  alu_secundaria_main main_4 (.ALU_Secundaria(PC), .out_2(out_16));
  Multiplexer #(.select(1), .width(7), .tristate("false")) multiplexer_1 (
    .in0(out_16), .in1(in_6), .out(multiplexer_1_out), .sel(in_8));

  // Notes on the sheet:
  //   ALU
  //   ALU2
endmodule
