// Logisim project mux_memoria.circ as structural Verilog: 1 circuit, main circuit main
module main (
  input  [6:0] EntradaPC,
  input  in_2,
  input  [6:0] EntradaIR,
  output [7:0] out_4
);

  wire [6:0] not_3_out;
  wire [7:0] adder_1_out;
  wire [7:7] not_1_out, not_2_out;

  not not_1 (not_1_out[7], 1'b1);
  not not_2 (not_2_out[7], 1'b1);
  not not_3 (not_3_out[0], 1'b1);
  not not_4 (not_3_out[1], 1'b1);
  not not_5 (not_3_out[2], 1'b1);
  not not_6 (not_3_out[3], 1'b1);
  not not_7 (not_3_out[4], 1'b1);
  not not_8 (not_3_out[5], 1'b1);
  not not_9 (not_3_out[6], 1'b1);
  Adder #(.width(8)) adder_1 (
    .a({not_1_out[7], EntradaPC}), .b({1'b1, not_3_out}), .out(adder_1_out));  // open: cin, cout
  Multiplexer #(.select(1), .width(8), .tristate("false")) multiplexer_1 (
    .in0(adder_1_out), .in1({not_2_out[7], EntradaIR}), .out(out_4), .sel(in_2));
endmodule
