// Logisim project mux_pc.circ as structural Verilog: 1 circuit, main circuit main
module main (
  input  [6:0] PC_incrementado,
  input  [6:0] IR,
  input  [1:0] in_3,
  input  [7:0] registro_e11,
  output [6:0] out_5
);

  Multiplexer #(.select(2), .width(7), .tristate("false")) multiplexer_1 (
    .in0(PC_incrementado), .in1(IR), .in2(registro_e11[6:0]), .out(out_5), .sel(in_3));  // open: in3

  // Notes on the sheet:
  //   00
  //   01
  //   10
endmodule
