// Logisim project mux_re.circ as structural Verilog: 1 circuit, main circuit main
module main (
  input  [6:0] in_1,
  input  in_2,
  input  [7:0] in_3,
  output [7:0] out_4
);

  wire [7:0] adder_1_out;
  wire [7:7] not_1_out;

  not not_1 (not_1_out[7], 1'b1);
  Adder #(.width(8)) adder_1 (.a({not_1_out[7], in_1}), .b(8'h1), .out(adder_1_out));  // open: cin, cout
  Multiplexer #(.select(1), .width(8)) multiplexer_1 (.in0(adder_1_out), .in1(in_3), .out(out_4), .sel(in_2));
endmodule
