// Logisim project pc.circ as structural Verilog: 1 circuit, main circuit main
module main (
  input  [6:0] in_1,
  input  in_2,
  output [6:0] out_3
);

  Register #(.width(7)) register_1 (.D(in_1), .Q(out_3), .clk(in_2));  // open: en, clr

  // Notes on the sheet:
  //   PC
endmodule
