// Logisim project pregunta.circ as structural Verilog: 1 circuit, main circuit main
module main (
  input  [3:0] in_1,
  input  [3:0] in_2,
  input  in_3,
  input  in_4,
  input  [7:0] in_5,
  input  in_6,
  output [7:0] out_7
);

  wire [3:0] multiplexer_1_out, register_1_q;

  Register #(.width(4)) register_1 (.D(in_1), .Q(register_1_q), .clk(in_4));  // open: en, clr
  registros_ultimo_main main_1 (.in_1(in_5), .out_4(out_7), .in_3(multiplexer_1_out), .in_2(in_6));
  Multiplexer #(.select(1), .width(4), .tristate("false")) multiplexer_1 (
    .in0(register_1_q), .in1(in_2), .out(multiplexer_1_out), .sel(in_3));
endmodule
