// Logisim project prueba.circ as structural Verilog: 1 circuit, main circuit main
module main (
  input  in_1,
  input  _1,
  input  _2,
  input  _3,
  input  _4,
  input  in_6,
  input  _5,
  input  _6,
  input  _7,
  input  _8,
  input  _9,
  input  _10,
  input  _11,
  input  _12,
  input  _13,
  input  _14,
  input  _15,
  input  _16,
  input  _17,
  output [7:0] out_20,
  output [11:0] out_21,
  output [1:0] out_22,
  output [7:0] out_23,
  output [3:0] out_24,
  output [7:0] out_25,
  output N,
  output Z,
  output D,
  output C
);

  wire clock_1_out, main_6_out_8, main_6_out_11, main_6_out_12, main_6_out_13, main_6_out_14, main_6_out_15,
       main_6_out_16, main_6_out_17, main_6_out_18, main_6_out_19, main_6_out_20, main_6_out_21,
       main_6_out_22, main_6_out_23, main_6_out_24, main_6_out_25, main_6_out_26, main_6_out_27,
       main_6_out_28, main_6_out_29, main_6_s1, main_6_s2, not_1_out, or_1_out, or_2_out, or_3_out, or_4_out,
       or_5_out, or_6_out, or_7_out, or_8_out, or_9_out, or_10_out, or_11_out, or_12_out, or_13_out,
       or_14_out, or_15_out, or_16_out, or_17_out;
  wire [3:0] controlled_buffer_1_out, main_5_r1, main_5_r2;
  wire [4:0] main_5_out_5;
  wire [6:0] main_1_out_5, main_3_out_2, main_4_out_3, main_5_direccion;
  wire [7:0] main_7_out_4, main_8_out_4, main_10_out_8, register_1_q, register_2_q;
  wire [11:0] controlled_buffer_4_out, main_2_out_3, main_13_out_2;

  Clock #(.highDuration(1), .lowDuration(1)) clock_1 (.out(clock_1_out));
  mux_pc_main main_1 (
    .PC_incrementado(main_3_out_2), .IR(main_5_direccion), .registro_e11(out_23), .in_3(out_22),
    .out_5(main_1_out_5));
  ir_main main_2 (.in_1(controlled_buffer_4_out), .in_2(or_7_out), .out_3(main_2_out_3));
  alu_secundaria_main main_3 (.ALU_Secundaria(main_4_out_3), .out_2(main_3_out_2));
  pc_main main_4 (.in_1(main_1_out_5), .in_2(or_4_out), .out_3(main_4_out_3));
  decodificadorIR_Memoria_main main_5 (
    .in_1(main_2_out_3), .Direccion(main_5_direccion), .R2(main_5_r2), .R1(main_5_r1), .out_5(main_5_out_5));
  Unidadcontrol_main main_6 (
    .in_3(clock_1_out), .out_11(main_6_out_11), .out_12(main_6_out_12), .out_13(main_6_out_13),
    .out_14(main_6_out_14), .out_15(main_6_out_15), .out_16(main_6_out_16), .out_17(main_6_out_17),
    .out_18(main_6_out_18), .out_19(main_6_out_19), .out_21(main_6_out_21), .out_23(main_6_out_23),
    .out_24(main_6_out_24), .out_25(main_6_out_25), .out_26(main_6_out_26), .out_27(main_6_out_27),
    .out_28(main_6_out_28), .in_2(in_6), .n(N), .z(Z), .d(C), .c(D), .in_1(main_5_out_5),
    .out_8(main_6_out_8), .s2(main_6_s2), .s1(main_6_s1), .out_20(main_6_out_20), .out_22(main_6_out_22),
    .out_29(main_6_out_29), .out_30(out_22));
  mux_memoria_main main_7 (
    .EntradaPC(main_4_out_3), .EntradaIR(main_5_direccion), .in_2(or_6_out), .out_4(main_7_out_4));
  mux_re_main main_8 (.in_1(main_4_out_3), .in_3(out_20), .in_2(or_5_out), .out_4(main_8_out_4));
  assign controlled_buffer_1_out = or_8_out ? 4'b1110 : 4'bz;  // Controlled_Buffer controlled_buffer_1
  assign controlled_buffer_1_out = or_9_out ? main_5_r2 : 4'bz;  // Controlled_Buffer controlled_buffer_2
  assign controlled_buffer_1_out = or_10_out ? main_5_r1 : 4'bz;  // Controlled_Buffer controlled_buffer_3
  registros_ultimo_main main_9 (.in_1(main_8_out_4), .out_4(out_23), .in_3(out_24), .in_2(or_12_out));
  Register #(.width(8)) register_1 (.D(out_23), .Q(register_1_q), .clk(or_13_out));  // open: en, clr
  ALU_main main_10 (
    .in_7(main_6_out_20), .S1(main_6_s1), .S2(main_6_s2), .Operando1(register_1_q), .Operando2(out_23),
    .in_6(main_6_out_8), .in_5(or_15_out), .out_8(main_10_out_8), .Resultado(out_25));
  Multiplexer #(.select(1), .width(4)) multiplexer_1 (
    .in0(4'b1111), .in1(controlled_buffer_1_out), .out(out_24), .sel(or_11_out));
  flags_main main_11 (.Entrada(main_10_out_8), .Selector(or_16_out), .N(N), .Z(Z), .D(C), .C(D));
  RAM #(.addrWidth(8), .dataWidth(12)) ram_1 (
    .addr(main_7_out_4), .data(out_21), .sel(or_1_out), .clk(or_2_out), .ld(or_3_out), .clr(in_1));
  assign controlled_buffer_4_out = or_3_out ? out_21 : 12'bz;  // Controlled_Buffer controlled_buffer_4
  not not_1 (not_1_out, or_3_out);
  assign main_8_out_4 = or_14_out ? register_2_q : 8'bz;  // Controlled_Buffer controlled_buffer_5
  Register #(.width(8)) register_2 (.D(out_25), .Q(register_2_q), .clk(or_15_out));  // open: en, clr
  assign out_21 = not_1_out ? main_13_out_2 : 12'bz;  // Controlled_Buffer controlled_buffer_6
  assign controlled_buffer_1_out = or_17_out ? 4'b1011 : 4'bz;  // Controlled_Buffer controlled_buffer_7
  conversorMemoria_registro_main main_12 (.in_1(controlled_buffer_4_out), .out_2(out_20));
  conversorRegistro_Memoria_main main_13 (.in_1(out_23), .out_2(main_13_out_2));
  or or_1 (or_1_out, main_6_out_11, _1);
  or or_2 (or_2_out, main_6_out_12, _2);
  or or_3 (or_3_out, main_6_out_13, _3);
  or or_4 (or_4_out, main_6_out_14, _4);
  or or_5 (or_5_out, main_6_out_15, _5);
  or or_6 (or_6_out, main_6_out_16, _6);
  or or_7 (or_7_out, main_6_out_17, _7);
  or or_8 (or_8_out, main_6_out_18, _8);
  or or_9 (or_9_out, main_6_out_19, _9);
  or or_10 (or_10_out, main_6_out_21, _10);
  or or_11 (or_11_out, main_6_out_23, _11);
  or or_12 (or_12_out, main_6_out_24, _12);
  or or_13 (or_13_out, main_6_out_25, _13);
  or or_14 (or_14_out, main_6_out_26, _14);
  or or_15 (or_15_out, main_6_out_27, _15);
  or or_16 (or_16_out, main_6_out_28, _16);
  or or_17 (or_17_out, main_6_out_29, _17);

  // Notes on the sheet:
  //   mux_pc
  //   ir
  //   7
  //   alu2
  //   pc
  //   4
  //   UC
  //   Mux_mem
  //   6
  //   5
  //   8
  //   r2
  //   r1
  //   9
  //   10
  //   13
  //   ALU
  //   2
  //   1
  //   3
  //   11
  //   Registros
  //   12
  //   15
  //   Flags
  //   16
  //   14
  //   Lo que hay en el registro
endmodule
