// Logisim project pruebamem.circ as structural Verilog: 1 circuit, main circuit main
module main (
  input  [11:0] in_1,
  input  in_2,
  input  in_3,
  input  in_4,
  input  in_5,
  output [15:0] out_6
);

  RAM #(.addrWidth(12), .dataWidth(16)) ram_1 (
    .addr(in_1), .data(out_6), .sel(in_2), .clk(in_3), .ld(in_4), .clr(in_5));
endmodule
