// Logisim project registros_ultimo.circ as structural Verilog: 1 circuit, main circuit main
module main (
  input  [7:0] in_1,
  input  in_2,
  input  [3:0] in_3,
  output [7:0] out_4
);

  wire decoder_1_out0, decoder_1_out1, decoder_1_out2, decoder_1_out3, decoder_1_out4, decoder_1_out5,
       decoder_1_out6, decoder_1_out7, decoder_1_out8, decoder_1_out9, decoder_1_out10, decoder_1_out11,
       decoder_1_out12, decoder_1_out13, decoder_1_out14, decoder_1_out15;
  wire [7:0] controlled_buffer_1_out, register_1_q, register_2_q, register_3_q, register_4_q, register_5_q,
       register_6_q, register_7_q, register_8_q, register_9_q, register_10_q, register_11_q, register_12_q,
       register_13_q, register_14_q, register_15_q, register_16_q;

  assign controlled_buffer_1_out = in_2 ? in_1 : 8'bz;  // Controlled_Buffer controlled_buffer_1
  Decoder #(.select(4), .tristate("false")) decoder_1 (
    .out0(decoder_1_out0), .out1(decoder_1_out1), .out2(decoder_1_out2), .out3(decoder_1_out3),
    .out4(decoder_1_out4), .out5(decoder_1_out5), .out6(decoder_1_out6), .out7(decoder_1_out7),
    .out8(decoder_1_out8), .out9(decoder_1_out9), .out10(decoder_1_out10), .out11(decoder_1_out11),
    .out12(decoder_1_out12), .out13(decoder_1_out13), .out14(decoder_1_out14), .out15(decoder_1_out15),
    .sel(in_3));
  Register #(.width(8)) register_1 (
    .D(controlled_buffer_1_out), .Q(register_1_q), .clk(decoder_1_out0));  // open: en, clr
  Register #(.width(8)) register_2 (
    .D(controlled_buffer_1_out), .Q(register_2_q), .clk(decoder_1_out1));  // open: en, clr
  assign out_4 = decoder_1_out0 ? register_1_q : 8'bz;  // Controlled_Buffer controlled_buffer_2
  assign out_4 = decoder_1_out1 ? register_2_q : 8'bz;  // Controlled_Buffer controlled_buffer_3
  Register #(.width(8)) register_3 (
    .D(controlled_buffer_1_out), .Q(register_3_q), .clk(decoder_1_out2));  // open: en, clr
  assign out_4 = decoder_1_out2 ? register_3_q : 8'bz;  // Controlled_Buffer controlled_buffer_4
  Register #(.width(8)) register_4 (
    .D(controlled_buffer_1_out), .Q(register_4_q), .clk(decoder_1_out3));  // open: en, clr
  Register #(.width(8)) register_5 (
    .D(controlled_buffer_1_out), .Q(register_5_q), .clk(decoder_1_out4));  // open: en, clr
  assign out_4 = decoder_1_out3 ? register_4_q : 8'bz;  // Controlled_Buffer controlled_buffer_5
  Register #(.width(8)) register_6 (
    .D(controlled_buffer_1_out), .Q(register_6_q), .clk(decoder_1_out5));  // open: en, clr
  assign out_4 = decoder_1_out4 ? register_5_q : 8'bz;  // Controlled_Buffer controlled_buffer_6
  assign out_4 = decoder_1_out5 ? register_6_q : 8'bz;  // Controlled_Buffer controlled_buffer_7
  Register #(.width(8)) register_7 (
    .D(controlled_buffer_1_out), .Q(register_7_q), .clk(decoder_1_out6));  // open: en, clr
  assign out_4 = decoder_1_out6 ? register_7_q : 8'bz;  // Controlled_Buffer controlled_buffer_8
  Register #(.width(8)) register_8 (
    .D(controlled_buffer_1_out), .Q(register_8_q), .clk(decoder_1_out7));  // open: en, clr
  Register #(.width(8)) register_9 (
    .D(controlled_buffer_1_out), .Q(register_9_q), .clk(decoder_1_out8));  // open: en, clr
  assign out_4 = decoder_1_out7 ? register_8_q : 8'bz;  // Controlled_Buffer controlled_buffer_9
  Register #(.width(8)) register_10 (
    .D(controlled_buffer_1_out), .Q(register_10_q), .clk(decoder_1_out9));  // open: en, clr
  assign out_4 = decoder_1_out8 ? register_9_q : 8'bz;  // Controlled_Buffer controlled_buffer_10
  assign out_4 = decoder_1_out9 ? register_10_q : 8'bz;  // Controlled_Buffer controlled_buffer_11
  Register #(.width(8)) register_11 (
    .D(controlled_buffer_1_out), .Q(register_11_q), .clk(decoder_1_out10));  // open: en, clr
  assign out_4 = decoder_1_out10 ? register_11_q : 8'bz;  // Controlled_Buffer controlled_buffer_12
  Register #(.width(8)) register_12 (
    .D(controlled_buffer_1_out), .Q(register_12_q), .clk(decoder_1_out11));  // open: en, clr
  Register #(.width(8)) register_13 (
    .D(controlled_buffer_1_out), .Q(register_13_q), .clk(decoder_1_out12));  // open: en, clr
  assign out_4 = decoder_1_out11 ? register_12_q : 8'bz;  // Controlled_Buffer controlled_buffer_13
  Register #(.width(8)) register_14 (
    .D(controlled_buffer_1_out), .Q(register_14_q), .clk(decoder_1_out13));  // open: en, clr
  assign out_4 = decoder_1_out12 ? register_13_q : 8'bz;  // Controlled_Buffer controlled_buffer_14
  assign out_4 = decoder_1_out13 ? register_14_q : 8'bz;  // Controlled_Buffer controlled_buffer_15
  Register #(.width(8)) register_15 (
    .D(controlled_buffer_1_out), .Q(register_15_q), .clk(decoder_1_out14));  // open: en, clr
  assign out_4 = decoder_1_out14 ? register_15_q : 8'bz;  // Controlled_Buffer controlled_buffer_16
  Register #(.width(8)) register_16 (
    .D(controlled_buffer_1_out), .Q(register_16_q), .clk(decoder_1_out15));  // open: en, clr
  assign out_4 = decoder_1_out15 ? register_16_q : 8'bz;  // Controlled_Buffer controlled_buffer_17
endmodule
