// Logisim project secuencia_cargar.circ as structural Verilog: 1 circuit, main circuit main
module main (
  input  in_1,
  input  reloj,
  input  in_3,
  output out_4,
  output _1,
  output _2,
  output _3,
  output _4,
  output _5,
  output _6,
  output _7,
  output _8,
  output _9,
  output _10,
  output _11,
  output _13,
  output _14,
  output _15,
  output _16,
  output _17,
  output _12
);

  wire d_ff_1_q, d_ff_5_q, d_ff_6_q, d_ff_7_q, d_ff_8_q, d_ff_9_q, d_ff_10_q, main_1_p2, main_2_p1,
       main_2_p2, main_3_p1, main_4_p1, main_5_p1;

  // _10señales_main main_1: pin names not known; wires that end beside it: out_4, main_1_p2, _1
  D_Flip_Flop d_ff_1 (.clk(reloj), .D(in_3), .Q(d_ff_1_q), .reset(in_1));  // open: Qn, preset, en
  // _10señales_main main_2: pin names not known; wires that end beside it: main_2_p1, main_2_p2, _3
  D_Flip_Flop d_ff_2 (.clk(reloj), .D(d_ff_1_q), .Q(main_1_p2), .reset(in_1));  // open: Qn, preset, en
  D_Flip_Flop d_ff_3 (.clk(reloj), .D(main_1_p2), .Q(main_2_p2), .reset(in_1));  // open: Qn, preset, en
  D_Flip_Flop d_ff_4 (.clk(reloj), .D(main_2_p1), .Q(out_4), .reset(in_1));  // open: Qn, preset, en
  D_Flip_Flop d_ff_5 (.clk(reloj), .D(main_2_p2), .Q(d_ff_5_q), .reset(in_1));  // open: Qn, preset, en
  // _10señales_main main_3: pin names not known; wires that end beside it: main_3_p1, d_ff_5_q, _5
  D_Flip_Flop d_ff_6 (.clk(reloj), .D(d_ff_5_q), .Q(d_ff_6_q), .reset(in_1));  // open: Qn, preset, en
  // _10señales_main main_4: pin names not known; wires that end beside it: main_4_p1, d_ff_1_q, _6
  D_Flip_Flop d_ff_7 (.clk(reloj), .D(d_ff_6_q), .Q(d_ff_7_q), .reset(in_1));  // open: Qn, preset, en
  D_Flip_Flop d_ff_8 (.clk(reloj), .D(d_ff_7_q), .Q(d_ff_8_q), .reset(in_1));  // open: Qn, preset, en
  D_Flip_Flop d_ff_9 (.clk(reloj), .D(d_ff_8_q), .Q(d_ff_9_q), .reset(in_1));  // open: Qn, preset, en
  // _10señales_main main_5: pin names not known; wires that end beside it: main_5_p1, d_ff_6_q, _8
  D_Flip_Flop d_ff_10 (.clk(reloj), .D(d_ff_9_q), .Q(d_ff_10_q), .reset(in_1));  // open: Qn, preset, en
  D_Flip_Flop d_ff_11 (.clk(reloj), .D(d_ff_10_q), .Q(main_5_p1), .reset(in_1));  // open: Qn, preset, en
  D_Flip_Flop d_ff_12 (.clk(reloj), .D(main_5_p1), .Q(main_3_p1), .reset(in_1));  // open: Qn, preset, en
  // _10señales_main main_6: pin names not known; wires that end beside it: d_ff_10_q, d_ff_8_q, _11
  D_Flip_Flop d_ff_13 (.clk(reloj), .D(main_3_p1), .Q(main_4_p1), .reset(in_1));  // open: Qn, preset, en
  D_Flip_Flop d_ff_14 (.clk(reloj), .D(main_4_p1), .Q(main_2_p1), .reset(in_1));  // open: Qn, preset, en
  // _10señales_main main_7: pin names not known; wires that end beside it: d_ff_9_q, d_ff_7_q, _12

  assign _2 = 1'b0;
  assign _4 = 1'b0;
  assign _7 = 1'b0;
  assign _9 = 1'b0;
  assign _10 = 1'b0;
  assign _13 = 1'b0;
  assign _14 = 1'b0;
  assign _15 = 1'b0;
  assign _16 = 1'b0;
  assign _17 = 1'b0;

  // Notes on the sheet:
  //   señal de cargar
  //   secuencua de señales de cargar
endmodule
