// Logisim project secuencia_estado0.circ as structural Verilog: 1 circuit, main circuit main
module main (
  input  reloj,
  input  in_2,
  input  in_3,
  output out_4,
  output _1,
  output _2,
  output _3,
  output _4,
  output _5,
  output _6,
  output _7,
  output _8,
  output _9,
  output _10,
  output _11,
  output _12,
  output _13,
  output _14,
  output _15,
  output _16
);

  wire d_ff_3_q, d_ff_4_q, main_1_p2, main_2_p1, main_2_p2;

  // _10señales_main main_1: pin names not known; wires that end beside it: out_4, main_1_p2, _1, _1
  D_Flip_Flop d_ff_1 (.clk(reloj), .D(in_2), .Q(main_1_p2), .reset(in_3));  // open: Qn, preset, en
  // _10señales_main main_2: pin names not known; wires that end beside it: main_2_p1, main_2_p2, _3
  D_Flip_Flop d_ff_2 (.clk(reloj), .D(main_1_p2), .Q(main_2_p2), .reset(in_3));  // open: Qn, preset, en
  D_Flip_Flop d_ff_3 (.clk(reloj), .D(main_2_p2), .Q(d_ff_3_q), .reset(in_3));  // open: Qn, preset, en
  D_Flip_Flop d_ff_4 (.clk(reloj), .D(d_ff_3_q), .Q(d_ff_4_q), .reset(in_3));  // open: Qn, preset, en
  D_Flip_Flop d_ff_5 (.clk(reloj), .D(d_ff_4_q), .Q(main_2_p1), .reset(in_3));  // open: Qn, preset, en
  D_Flip_Flop d_ff_6 (.clk(reloj), .D(main_2_p1), .Q(out_4), .reset(in_3));  // open: Qn, preset, en
  // _10señales_main main_3: pin names not known; wires that end beside it: d_ff_4_q, d_ff_3_q, _7

  assign _2 = 1'b0;
  assign _4 = 1'b0;
  assign _5 = 1'b0;
  assign _6 = 1'b0;
  assign _8 = 1'b0;
  assign _9 = 1'b0;
  assign _10 = 1'b0;
  assign _11 = 1'b0;
  assign _12 = 1'b0;
  assign _13 = 1'b0;
  assign _14 = 1'b0;
  assign _15 = 1'b0;
  assign _16 = 1'b0;

  // Notes on the sheet:
  //   señal de estado 0
  //   secuencua de señales de estado 0
endmodule
