// Logisim project secuencia_inc_PC.circ as structural Verilog: 1 circuit, main circuit main
module main (
  input  in_1,
  input  in_2,
  input  in_3,
  output out_4,
  output _4
);

  wire d_ff_1_q;

  D_Flip_Flop d_ff_1 (.clk(in_1), .D(in_2), .Q(d_ff_1_q), .reset(in_3));  // open: Qn, preset, en
  D_Flip_Flop d_ff_2 (.clk(in_1), .D(d_ff_1_q), .Q(out_4), .reset(in_3));  // open: Qn, preset, en
  // _10señales_main main_1: pin names not known; wires that end beside it: out_4, d_ff_1_q, _4
endmodule
