// Logisim project secuencia_inversor.circ as structural Verilog: 1 circuit, main circuit main
module main (
  input  in_1,
  input  reloj,
  input  in_3,
  output out_4,
  output _1,
  output _2,
  output _3,
  output _4,
  output _5,
  output _6,
  output _7,
  output _8,
  output _9,
  output _10,
  output _13,
  output _14,
  output _15,
  output _16,
  output _12,
  output _11
);

  wire d_ff_1_q, d_ff_2_q, d_ff_3_q, d_ff_4_q, d_ff_5_q, d_ff_6_q, d_ff_7_q, d_ff_8_q, d_ff_9_q, d_ff_10_q,
       d_ff_11_q, d_ff_12_q, d_ff_13_q, d_ff_14_q, d_ff_15_q, d_ff_16_q, d_ff_19_q, main_2_p2, main_4_p3,
       main_5_p2, main_5_p3;

  D_Flip_Flop d_ff_1 (.clk(reloj), .D(in_3), .Q(d_ff_1_q), .reset(in_1));  // open: Qn, preset, en
  D_Flip_Flop d_ff_2 (.clk(reloj), .D(d_ff_1_q), .Q(d_ff_2_q), .reset(in_1));  // open: Qn, preset, en
  D_Flip_Flop d_ff_3 (.clk(reloj), .D(d_ff_2_q), .Q(d_ff_3_q), .reset(in_1));  // open: Qn, preset, en
  D_Flip_Flop d_ff_4 (.clk(reloj), .D(d_ff_3_q), .Q(d_ff_4_q), .reset(in_1));  // open: Qn, preset, en
  // _10señales_main main_1: pin names not known; wires that end beside it: out_4, d_ff_1_q, _5, _5
  D_Flip_Flop d_ff_5 (.clk(reloj), .D(main_5_p2), .Q(d_ff_5_q), .reset(in_1));  // open: Qn, preset, en
  D_Flip_Flop d_ff_6 (.clk(reloj), .D(d_ff_4_q), .Q(d_ff_6_q), .reset(in_1));  // open: Qn, preset, en
  D_Flip_Flop d_ff_7 (.clk(reloj), .D(d_ff_5_q), .Q(d_ff_7_q), .reset(in_1));  // open: Qn, preset, en
  D_Flip_Flop d_ff_8 (.clk(reloj), .D(d_ff_6_q), .Q(d_ff_8_q), .reset(in_1));  // open: Qn, preset, en
  D_Flip_Flop d_ff_9 (.clk(reloj), .D(d_ff_7_q), .Q(d_ff_9_q), .reset(in_1));  // open: Qn, preset, en
  D_Flip_Flop d_ff_10 (.clk(reloj), .D(d_ff_8_q), .Q(d_ff_10_q), .reset(in_1));  // open: Qn, preset, en
  D_Flip_Flop d_ff_11 (.clk(reloj), .D(d_ff_9_q), .Q(d_ff_11_q), .reset(in_1));  // open: Qn, preset, en
  D_Flip_Flop d_ff_12 (.clk(reloj), .D(d_ff_10_q), .Q(d_ff_12_q), .reset(in_1));  // open: Qn, preset, en
  D_Flip_Flop d_ff_13 (.clk(reloj), .D(d_ff_11_q), .Q(d_ff_13_q), .reset(in_1));  // open: Qn, preset, en
  D_Flip_Flop d_ff_14 (.clk(reloj), .D(d_ff_12_q), .Q(d_ff_14_q), .reset(in_1));  // open: Qn, preset, en
  // _10señales_main main_2: pin names not known; wires that end beside it: d_ff_9_q, main_2_p2, _9
  D_Flip_Flop d_ff_15 (.clk(reloj), .D(d_ff_14_q), .Q(d_ff_15_q), .reset(in_1));  // open: Qn, preset, en
  // _10señales_main main_3: pin names not known; wires that end beside it: d_ff_10_q, d_ff_2_q, _10, _10
  D_Flip_Flop d_ff_16 (.clk(reloj), .D(d_ff_13_q), .Q(d_ff_16_q), .reset(in_1));  // open: Qn, preset, en
  D_Flip_Flop d_ff_17 (.clk(reloj), .D(d_ff_15_q), .Q(main_2_p2), .reset(in_1));  // open: Qn, preset, en
  // _10señales_main main_4: pin names not known; wires that end beside it: d_ff_8_q, d_ff_3_q, main_4_p3
  or or_1 (_11, main_4_p3, main_5_p3);
  D_Flip_Flop d_ff_18 (.clk(reloj), .D(d_ff_16_q), .Q(out_4), .reset(in_1));  // open: Qn, preset, en
  D_Flip_Flop d_ff_19 (.clk(reloj), .D(main_2_p2), .Q(d_ff_19_q), .reset(in_1));  // open: Qn, preset, en
  // _10señales_main main_5: pin names not known; wires that end beside it: d_ff_7_q, main_5_p2, main_5_p3
  D_Flip_Flop d_ff_20 (.clk(reloj), .D(d_ff_19_q), .Q(main_5_p2), .reset(in_1));  // open: Qn, preset, en
  // _10señales_main main_6: pin names not known; wires that end beside it: d_ff_5_q, d_ff_19_q, _12
  // _10señales_main main_7: pin names not known; wires that end beside it: d_ff_6_q, d_ff_4_q, _13
  // _10señales_main main_8: pin names not known; wires that end beside it: d_ff_11_q, d_ff_15_q, _14
  // _10señales_main main_9: pin names not known; wires that end beside it: d_ff_14_q, d_ff_12_q, _15
  // _10señales_main main_10: pin names not known; wires that end beside it: d_ff_16_q, d_ff_13_q, _16

  assign _1 = 1'b0;
  assign _2 = 1'b0;
  assign _3 = 1'b0;
  assign _4 = 1'b0;
  assign _6 = 1'b0;
  assign _7 = 1'b0;
  assign _8 = 1'b0;

  // Notes on the sheet:
  //   señal del inversor
  //   secuencua dl inversor
endmodule
