// Logisim project secuencia_saltos.circ as structural Verilog: 1 circuit, main circuit main
module main (
  input  in_1,
  input  in_2,
  input  in_3,
  output out_4,
  output _1,
  output _2,
  output _3,
  output _4,
  output _5,
  output _6,
  output _7,
  output _8,
  output _9,
  output _10,
  output _11,
  output _12,
  output _13,
  output _14,
  output _15,
  output _16,
  output _17,
  output [1:0] _18
);

  wire d_ff_1_q, d_ff_2_q, d_ff_3_q;

  D_Flip_Flop d_ff_1 (.clk(in_1), .D(in_2), .Q(d_ff_1_q), .reset(in_3));  // open: Qn, preset, en
  D_Flip_Flop d_ff_2 (.clk(in_1), .D(d_ff_1_q), .Q(d_ff_2_q), .reset(in_3));  // open: Qn, preset, en
  D_Flip_Flop d_ff_3 (.clk(in_1), .D(d_ff_2_q), .Q(d_ff_3_q), .reset(in_3));  // open: Qn, preset, en
  // _10señales_main main_1: pin names not known; wires that end beside it: d_ff_3_q, d_ff_2_q, _4
  D_Flip_Flop d_ff_4 (.clk(in_1), .D(d_ff_3_q), .Q(out_4), .reset(in_3));  // open: Qn, preset, en
  // _10señales_main main_2: pin names not known; wires that end beside it: 1'b0, out_4, d_ff_1_q, _18[0]

  assign _1 = 1'b0;
  assign _2 = 1'b0;
  assign _3 = 1'b0;
  assign _5 = 1'b0;
  assign _6 = 1'b0;
  assign _7 = 1'b0;
  assign _8 = 1'b0;
  assign _9 = 1'b0;
  assign _10 = 1'b0;
  assign _11 = 1'b0;
  assign _12 = 1'b0;
  assign _13 = 1'b0;
  assign _14 = 1'b0;
  assign _15 = 1'b0;
  assign _16 = 1'b0;
  assign _17 = 1'b0;
  assign _18[1] = 1'b0;
endmodule
