// Logisim project secuencias.circ as structural Verilog: 1 circuit, main circuit main
module main (
  input  reloj,
  input  in_2,
  input  in_3,
  input  in_4,
  input  in_5,
  input  in_6,
  input  in_7,
  input  in_8,
  input  in_9,
  input  in_10,
  input  in_11,
  input  in_12,
  output inc_pc,
  output out_14,
  output out_15,
  output out_16,
  output out_17,
  output out_18,
  output out_19,
  output out_20,
  output out_21,
  output out_22,
  output out_23,
  output out_24,
  output out_25,
  output out_26,
  output out_27,
  output out_28,
  output out_29,
  output out_30,
  output out_31,
  output out_32,
  output [1:0] out_33
);

  wire main_1_out_4, main_2_out_4, main_3_out_4, main_4_out_4, main_5_out_4, main_6_out_4, main_7_out_4,
       main_8_out_4, main_10_out_4, or_3_out, or_4_out;
  wire [1:0] main_5__18;
  wire [15:15] main_8__4;
  wire [18:0] main_2__17, main_4__17, or_1_out;
  wire [18:2] main_5__17, main_7__17;
  wire [18:3] main_1__16, main_3__16, main_6__16, main_9__16, main_10__16;

  secuencia_ope_sum_y_o_main main_1 (
    .reloj(reloj), .in_3(in_3), .in_1(in_2), ._1(main_1__16[18]), ._2(main_1__16[17]), ._3(main_1__16[16]),
    ._4(main_1__16[15]), ._5(main_1__16[14]), ._6(main_1__16[13]), ._7(main_1__16[12]), ._8(main_1__16[11]),
    ._9(main_1__16[10]), ._10(main_1__16[9]), ._11(main_1__16[8]), ._12(main_1__16[7]), ._13(main_1__16[6]),
    ._14(main_1__16[5]), ._15(main_1__16[4]), ._16(main_1__16[3]), .out_4(main_1_out_4));
  secuencia_invocar_main main_2 (
    .reloj(reloj), .in_2(in_8), .in_3(in_2), ._1(main_2__17[18]), ._2(main_2__17[17]), ._3(main_2__17[16]),
    ._4(main_2__17[15]), ._5(main_2__17[14]), ._6(main_2__17[13]), ._7(main_2__17[12]), ._8(main_2__17[11]),
    ._9(main_2__17[10]), ._10(main_2__17[9]), ._11(main_2__17[8]), ._12(main_2__17[7]), ._13(main_2__17[6]),
    ._14(main_2__17[5]), ._15(main_2__17[4]), ._16(main_2__17[3]), ._17(main_2__17[2]),
    ._18(main_2__17[1:0]), .out_4(main_2_out_4));
  assign or_1_out = {main_1__16, 3'b000} | {main_3__16, 3'b000} | {main_5__17, main_5__18} | {main_7__17, 2'b00} | {main_10__16, 3'b000} | main_2__17 | main_4__17 | {main_6__16, 3'b000} | {main_9__16, 3'b000};  // OR_Gate or_1, 19 bits wide
  assign {out_16, out_17, out_18, out_19, out_20, out_21, out_22, out_23, out_24, out_25, out_26, out_27, out_28, out_29, out_30, out_31, out_32, out_33} = {3'b000, main_8__4[15], {15{1'b0}}} | or_1_out;  // OR_Gate or_2, 19 bits wide
  secuencia_inversor_main main_3 (
    .reloj(reloj), .in_3(in_4), .in_1(in_2), ._1(main_3__16[18]), ._2(main_3__16[17]), ._3(main_3__16[16]),
    ._4(main_3__16[15]), ._5(main_3__16[14]), ._6(main_3__16[13]), ._7(main_3__16[12]), ._8(main_3__16[11]),
    ._9(main_3__16[10]), ._10(main_3__16[9]), ._11(main_3__16[8]), ._12(main_3__16[7]), ._13(main_3__16[6]),
    ._14(main_3__16[5]), ._15(main_3__16[4]), ._16(main_3__16[3]), .out_4(main_3_out_4));
  secuencia_retorno_main main_4 (
    .reloj(reloj), .in_2(in_9), .in_3(in_2), ._1(main_4__17[18]), ._2(main_4__17[17]), ._3(main_4__17[16]),
    ._4(main_4__17[15]), ._5(main_4__17[14]), ._6(main_4__17[13]), ._7(main_4__17[12]), ._8(main_4__17[11]),
    ._9(main_4__17[10]), ._10(main_4__17[9]), ._11(main_4__17[8]), ._12(main_4__17[7]), ._13(main_4__17[6]),
    ._14(main_4__17[5]), ._15(main_4__17[4]), ._16(main_4__17[3]), ._17(main_4__17[2]),
    ._18(main_4__17[1:0]), .out_4(main_4_out_4));
  secuencia_saltos_main main_5 (
    .in_1(reloj), .in_2(in_5), .in_3(in_2), ._1(main_5__17[18]), ._2(main_5__17[17]), ._3(main_5__17[16]),
    ._4(main_5__17[15]), ._5(main_5__17[14]), ._6(main_5__17[13]), ._7(main_5__17[12]), ._8(main_5__17[11]),
    ._9(main_5__17[10]), ._10(main_5__17[9]), ._11(main_5__17[8]), ._12(main_5__17[7]), ._13(main_5__17[6]),
    ._14(main_5__17[5]), ._15(main_5__17[4]), ._16(main_5__17[3]), ._17(main_5__17[2]), ._18(main_5__18),
    .out_4(main_5_out_4));
  secuencia_mover_main main_6 (
    .reloj(reloj), .in_3(in_10), .in_1(in_2), ._1(main_6__16[18]), ._2(main_6__16[17]), ._3(main_6__16[16]),
    ._4(main_6__16[15]), ._5(main_6__16[14]), ._6(main_6__16[13]), ._7(main_6__16[12]), ._8(main_6__16[11]),
    ._9(main_6__16[10]), ._10(main_6__16[9]), ._11(main_6__16[8]), ._12(main_6__16[7]), ._13(main_6__16[6]),
    ._14(main_6__16[5]), ._15(main_6__16[4]), ._16(main_6__16[3]), .out_4(main_6_out_4));
  secuencia_cargar_main main_7 (
    .reloj(reloj), .in_3(in_6), .in_1(in_2), ._1(main_7__17[18]), ._2(main_7__17[17]), ._3(main_7__17[16]),
    ._4(main_7__17[15]), ._5(main_7__17[14]), ._6(main_7__17[13]), ._7(main_7__17[12]), ._8(main_7__17[11]),
    ._9(main_7__17[10]), ._10(main_7__17[9]), ._11(main_7__17[8]), ._12(main_7__17[7]), ._13(main_7__17[6]),
    ._14(main_7__17[5]), ._15(main_7__17[4]), ._16(main_7__17[3]), ._17(main_7__17[2]), .out_4(main_7_out_4));
  secuencia_inc_PC_main main_8 (.in_1(reloj), .in_2(in_12), .in_3(in_2), ._4(main_8__4[15]), .out_4(main_8_out_4));
  secuencia_estado0_main main_9 (
    .reloj(reloj), .in_2(in_11), .in_3(in_2), ._1(main_9__16[18]), ._2(main_9__16[17]), ._3(main_9__16[16]),
    ._4(main_9__16[15]), ._5(main_9__16[14]), ._6(main_9__16[13]), ._7(main_9__16[12]), ._8(main_9__16[11]),
    ._9(main_9__16[10]), ._10(main_9__16[9]), ._11(main_9__16[8]), ._12(main_9__16[7]), ._13(main_9__16[6]),
    ._14(main_9__16[5]), ._15(main_9__16[4]), ._16(main_9__16[3]), .out_4(out_15));
  secuencia_guardar_main main_10 (
    .reloj(reloj), .in_2(in_7), .in_3(in_2), ._1(main_10__16[18]), ._2(main_10__16[17]),
    ._3(main_10__16[16]), ._4(main_10__16[15]), ._5(main_10__16[14]), ._6(main_10__16[13]),
    ._7(main_10__16[12]), ._8(main_10__16[11]), ._9(main_10__16[10]), ._10(main_10__16[9]),
    ._11(main_10__16[8]), ._12(main_10__16[7]), ._13(main_10__16[6]), ._14(main_10__16[5]),
    ._15(main_10__16[4]), ._16(main_10__16[3]), .out_4(main_10_out_4));
  or or_3 (or_3_out, main_7_out_4, main_10_out_4, main_5_out_4, main_3_out_4, main_1_out_4);
  or or_4 (or_4_out, main_2_out_4, main_4_out_4, main_6_out_4, out_15, main_8_out_4);
  // OR_Gate or_5 has open pins: in0=or_3_out, in2=or_4_out, out=open
  or or_6 (inc_pc, main_1_out_4, main_3_out_4, main_7_out_4, main_10_out_4, main_6_out_4, main_1_out_4);
  or or_7 (out_14, main_5_out_4, main_8_out_4, main_2_out_4, main_4_out_4);

  // Notes on the sheet:
  //   invocar
  //   suma_Y_O
  //   inversor
  //   retorno
  //   saltos
  //   mover
  //   cargar
  //   estado0
  //   incpc
  //   guardar
  //   despues de lectura ir decodificarla
  //   reset despues de inc_pc o llamada o salto
endmodule
