// Logisim project EJ.circ as structural Verilog: 1 circuit, main circuit main
module main (
  input  in_1
);

  wire clock_1_out, controlled_buffer_1_out;
  wire [7:0] counter_1_q, random_1_out;

  Clock clock_1 (.out(clock_1_out));
  Counter counter_1 (.Q(counter_1_q), .clk(controlled_buffer_1_out));  // open: load, D, count, carry, clr
  Random random_1 (.clk(clock_1_out), .out(random_1_out));  // open: next, clr
  RAM #(.bus("separate")) ram_1 (
    .addr(counter_1_q), .din(random_1_out), .clk(controlled_buffer_1_out));  // open: data, str, sel, ld, clr
  assign controlled_buffer_1_out = in_1 ? clock_1_out : 1'bz;  // Controlled_Buffer controlled_buffer_1

  // Notes on the sheet:
  //   counter
  //   random generator
  //   ram
  //   bufer controlado
endmodule
